// Logisim project CPU.circ as structural Verilog
module CPU (
  input  _0,
  input  _1,
  input  _2,
  input  _3,
  input  Enable_Program_Write,
  input  Auto_Clock,
  input  One_by_One,
  input  in_8,
  input  in_9,
  input  in_10,
  input  in_11,
  input  in_12,
  input  in_13,
  input  in_14,
  input  in_15,
  input  in_16,
  input  in_17,
  input  in_18
);

  wire Accumulator__7_2, alu_1_a_greater_b, alu_1_b_greater_a, alu_1_not_equal, alu_1_overflow, alu_1_x0,
       alu_1_x1, alu_1_x2, alu_1_x3, alu_1_x4, alu_1_x5, alu_1_x6, alu_1_x7, alu_1_zero, and_1_out,
       and_2_out, and_3_out, and_4_out, and_5_out, and_6_out, and_7_out, and_8_out, and_9_out, buffer_1_out,
       buffer_2_out, buffer_3_out, buffer_4_out, buffer_5_out, buffer_6_out, buffer_7_out, Clear_Input_out,
       condition_code_register_1_a_greater_b_2, condition_code_register_1_b_greater_a_2,
       condition_code_register_1_finished_2, condition_code_register_1_negative_2,
       condition_code_register_1_not_equal_2, condition_code_register_1_overflow_2,
       condition_code_register_1_waiting_2, condition_code_register_1_zero_2, control_panel_1_clock,
       control_panel_1_enable_write, control_panel_1_next_instruction_2, control_panel_1_one_by_one_2,
       control_panel_1_program_reset_out, control_panel_1_reset_out, control_panel_1_system_clock,
       control_panel_1_write_next_byte, control_unit_1_a, control_unit_1_a_clock, control_unit_1_a_invert,
       control_unit_1_a_reset, control_unit_1_aa_reset, control_unit_1_ab_reset, control_unit_1_acc_a_clock,
       control_unit_1_acc_b_clock, control_unit_1_acc_x_clock, control_unit_1_acc_y_clock,
       control_unit_1_add, control_unit_1_and, control_unit_1_ax_reset, control_unit_1_ay_reset,
       control_unit_1_b, control_unit_1_b_invert, control_unit_1_clock_b_greater_a, control_unit_1_clock_ccr,
       control_unit_1_display_clock, control_unit_1_increment, control_unit_1_ir_clock,
       control_unit_1_ir_reset, control_unit_1_m_clock, control_unit_1_mar_clock, control_unit_1_mar_reset,
       control_unit_1_mbr_clock, control_unit_1_mbr_reset, control_unit_1_mp_alu_a_s0,
       control_unit_1_mp_alu_a_s1, control_unit_1_mp_alu_b_s0, control_unit_1_mp_alu_b_s1,
       control_unit_1_mp_mar_s0, control_unit_1_mp_mar_s1, control_unit_1_mp_mar_s2, control_unit_1_mp_pc_s0,
       control_unit_1_mp_pc_s1, control_unit_1_multiply, control_unit_1_or, control_unit_1_pc_count,
       control_unit_1_pc_set, control_unit_1_read_input, control_unit_1_reset_io,
       control_unit_1_set_mar_add_mbr, control_unit_1_shift_a_left, control_unit_1_shift_a_right,
       control_unit_1_shift_b_left, control_unit_1_shift_b_right, control_unit_1_shift_loop,
       control_unit_1_stack_pop, control_unit_1_stack_push, control_unit_1_stack_reset,
       control_unit_1_x_invert, control_unit_1_xor, controlled_buffer_5_x0, controlled_buffer_5_x1,
       controlled_buffer_5_x2, controlled_buffer_5_x3, controlled_buffer_5_x4, controlled_buffer_5_x5,
       controlled_buffer_5_x6, controlled_buffer_5_x7, IR__0_3, IR__1_2, IR__2_2, IR__3_2, IR__4_2, IR__5_2,
       IR__6_2, IR__7_2, keyboard_1_avail, MAR__0_3, MAR__1_2, MAR__2_2, MAR__3_2, MAR__4_2, MAR__5_2,
       MAR__6_2, MAR__7_2, MBR__0_3, MBR__1_2, MBR__2_2, MBR__3_2, MBR__4_2, MBR__5_2, MBR__6_2, MBR__7_2,
       n3_way_multiplexor_1__0_4, n3_way_multiplexor_1__1_4, n3_way_multiplexor_1__2_4,
       n3_way_multiplexor_1__3_4, n3_way_multiplexor_1__4_4, n3_way_multiplexor_1__5_4,
       n3_way_multiplexor_1__6_4, n3_way_multiplexor_1__7_4, n3_way_multiplexor_2__0_4,
       n3_way_multiplexor_2__1_4, n3_way_multiplexor_2__2_4, n3_way_multiplexor_2__3_4,
       n3_way_multiplexor_2__4_4, n3_way_multiplexor_2__5_4, n3_way_multiplexor_2__6_4,
       n3_way_multiplexor_2__7_4, n3_way_multiplexor_4__0_4, n3_way_multiplexor_4__1_4,
       n3_way_multiplexor_4__2_4, n3_way_multiplexor_4__3_4, n3_way_multiplexor_4__4_4,
       n3_way_multiplexor_4__5_4, n3_way_multiplexor_4__6_4, n3_way_multiplexor_4__7_4,
       n5_way_multiplexer_1__0_6, n5_way_multiplexer_1__1_6, n5_way_multiplexer_1__2_6,
       n5_way_multiplexer_1__3_6, n5_way_multiplexer_1__4_6, n5_way_multiplexer_1__5_6,
       n5_way_multiplexer_1__6_6, n5_way_multiplexer_1__7_6, n8_bit_adder_1_x0, n8_bit_adder_1_x1,
       n8_bit_adder_1_x2, n8_bit_adder_1_x3, n8_bit_adder_1_x4, n8_bit_adder_1_x5, n8_bit_adder_1_x6,
       n8_bit_adder_1_x7, n8_bit_counter_3_increment_out, n8_bit_counter_3_set_carry,
       n8_bit_counter_4_increment_out, n8_bit_counter_4_set_carry, n8_bit_counter_5_increment_out,
       n8_bit_counter_5_set_carry, n8_bit_stack_1__0_2, n8_bit_stack_1__1_2, n8_bit_stack_1__2_2,
       n8_bit_stack_1__3_2, n8_bit_stack_1__4_2, n8_bit_stack_1__5_2, n8_bit_stack_1__6_2,
       n8_bit_stack_1__7_2, Next_Instruction_out, not_1_out, or_1_out, or_2_out, or_3_out, PC__0_2, PC__1_2,
       PC__2_2, PC__3_2, PC__4_2, PC__5_2, PC__6_2, PC__7_2, Program_Reset_out, Register_A__0_3,
       Register_A__1_2, Register_A__2_2, Register_A__3_2, Register_A__4_2, Register_A__5_2, Register_A__6_2,
       Register_A__7_2, Register_B__0_3, Register_B__1_2, Register_B__2_2, Register_B__3_2, Register_B__4_2,
       Register_B__5_2, Register_B__6_2, Register_B__7_2, Register_X__0_3, Register_X__1_2, Register_X__2_2,
       Register_X__3_2, Register_X__4_2, Register_X__5_2, Register_X__6_2, Register_X__7_2, Register_Y__0_3,
       Register_Y__1_2, Register_Y__2_2, Register_Y__3_2, Register_Y__4_2, Register_Y__5_2, Register_Y__6_2,
       Register_Y__7_2, Reset_out, Tick_out, undriven, undriven_2, undriven_3, undriven_4, Write_Byte_out,
       x_1__0_2, x_1__1_2, x_1__2_2, x_1__3_2, x_1__4_2, x_1__5_2, x_1__6_2, x_1__7_2, x_2__0_2, x_2__1_2,
       x_2__2_2, x_2__3_2, x_2__4_2, x_2__5_2, x_2__6_2, x_2__7_2, x_3__0_2, x_3__1_2, x_3__2_2, x_3__3_2,
       x_3__4_2, x_3__5_2, x_3__6_2, x_3__7_2, x_4__0_2, x_4__1_2, x_4__2_2, x_4__3_2, x_4__4_2, x_4__5_2,
       x_4__6_2, x_4__7_2;
  wire [3:0] joystick_1_x, joystick_1_y, n8_bit_counter_2__0_2, n8_bit_counter_2__4_2, n8_bit_counter_3__0_2,
       n8_bit_counter_3__4_2, n8_bit_counter_4__0_2, n8_bit_counter_4__4_2, n8_bit_counter_5__0_2,
       n8_bit_counter_5__4_2;
  wire [6:0] Accumulator__0_3, keyboard_1_data;
  wire [7:0] Accumulator__0_2, controlled_buffer_1_out, IR__0_2, MAR__0_2, MBR__0_2, multiplexer_1_out,
       n2_way_multiplexor_1__0_3, n3_way_multiplexor_3__0_4, n8_bit_counter_1__0_2, ram_1_data,
       Register_A__0_2, Register_B__0_2, Register_X__0_2, Register_Y__0_2, rom_1_data, rom_2_data,
       rom_3_data, rom_4_data;
  wire [15:0] led_matrix_controller_1_out_12, led_matrix_controller_1_out_13, led_matrix_controller_1_out_14,
       led_matrix_controller_1_out_15, led_matrix_controller_1_out_16, led_matrix_controller_1_out_17,
       led_matrix_controller_1_out_18, led_matrix_controller_1_out_19, led_matrix_controller_1_out_20,
       led_matrix_controller_1_out_21, led_matrix_controller_1_out_22, led_matrix_controller_1_out_23,
       led_matrix_controller_1_out_24, led_matrix_controller_1_out_25, led_matrix_controller_1_out_26,
       led_matrix_controller_1_out_27;

  _7_Way_Multiplexor u_7_way_multiplexor_1 ();  // open: A0, _1, _2, _3, _4, _5, _6, _7, B0, _1_2, _2_2, _3_2, _4_2, _5_2, _6_2, _7_2, C0, _1_3, _2_3, _3_3, _4_3, _5_3, _6_3, _7_3, D0, _1_4, _2_4, _3_4, _4_4, _5_4, _6_4, _7_4, E0, _1_5, _2_5, _3_5, _4_5, _5_5, _6_5, _7_5, F0, _1_6, _2_6, _3_6, _4_6, _5_6, _6_6, _7_6, G0, _1_7, _2_7, _3_7, _4_7, _5_7, _6_7, _7_7, S2, S1, S0, _7_8, _6_8, _5_8, _4_8, _3_8, _2_8, _1_8, _0
  buf buffer_1 (buffer_1_out, and_1_out);
  buf buffer_2 (buffer_2_out, buffer_1_out);
  buf buffer_3 (buffer_3_out, buffer_2_out);
  buf buffer_4 (buffer_4_out, buffer_3_out);
  buf buffer_5 (buffer_5_out, buffer_4_out);
  buf buffer_6 (buffer_6_out, buffer_5_out);
  buf buffer_7 (buffer_7_out, buffer_6_out);
  not not_1 (not_1_out, and_2_out);
  and and_1 (and_1_out, not_1_out, control_panel_1_write_next_byte);
  and and_2 (and_2_out, n8_bit_counter_1__0_2[0], and_3_out);
  ROM rom_1 (.addr(n8_bit_counter_1__0_2), .data(rom_1_data));  // open: sel
  assign controlled_buffer_1_out = _0 ? rom_1_data : 8'bz;  // Controlled_Buffer_part controlled_buffer_1
  and and_3 (and_3_out, n8_bit_counter_1__0_2[1], and_4_out);
  and and_4 (and_4_out, n8_bit_counter_1__0_2[2], and_5_out);
  and and_5 (and_5_out, n8_bit_counter_1__0_2[3], and_6_out);
  or or_1 (or_1_out, buffer_7_out, control_unit_1_m_clock);
  _8_bit_Register Register_A (
    ._7(Accumulator__7_2), ._6(Accumulator__0_3[6]), ._5(Accumulator__0_3[5]), ._4(Accumulator__0_3[4]),
    ._3(Accumulator__0_3[3]), ._2(Accumulator__0_3[2]), ._1(Accumulator__0_3[1]), ._0(Accumulator__0_3[0]),
    ._0_3(Register_A__0_3), ._1_2(Register_A__1_2), ._2_2(Register_A__2_2), ._3_2(Register_A__3_2),
    ._4_2(Register_A__4_2), ._5_2(Register_A__5_2), ._6_2(Register_A__6_2), ._7_2(Register_A__7_2),
    .Clock(control_unit_1_acc_a_clock), .Reset(control_unit_1_aa_reset), ._0_2(Register_A__0_2));
  // Probe on Register_A__0_2
  and and_6 (and_6_out, n8_bit_counter_1__0_2[4], and_7_out);
  and and_7 (and_7_out, n8_bit_counter_1__0_2[5], and_8_out);
  RAM #(.bus("separate")) ram_1 (
    .addr(n2_way_multiplexor_1__0_3), .din(n3_way_multiplexor_3__0_4), .data(ram_1_data), .clk(or_1_out),
    .clr(control_panel_1_program_reset_out));  // open: str, sel, ld
  _8_bit_Register Register_X (
    ._7(Accumulator__7_2), ._6(Accumulator__0_3[6]), ._5(Accumulator__0_3[5]), ._4(Accumulator__0_3[4]),
    ._3(Accumulator__0_3[3]), ._2(Accumulator__0_3[2]), ._1(Accumulator__0_3[1]), ._0(Accumulator__0_3[0]),
    ._0_3(Register_X__0_3), ._1_2(Register_X__1_2), ._2_2(Register_X__2_2), ._3_2(Register_X__3_2),
    ._4_2(Register_X__4_2), ._5_2(Register_X__5_2), ._6_2(Register_X__6_2), ._7_2(Register_X__7_2),
    .Clock(control_unit_1_acc_x_clock), .Reset(control_unit_1_ax_reset), ._0_2(Register_X__0_2));
  // Probe on Register_X__0_2
  _8_bit_Register Register_B (
    ._7(Accumulator__7_2), ._6(Accumulator__0_3[6]), ._5(Accumulator__0_3[5]), ._4(Accumulator__0_3[4]),
    ._3(Accumulator__0_3[3]), ._2(Accumulator__0_3[2]), ._1(Accumulator__0_3[1]), ._0(Accumulator__0_3[0]),
    ._0_3(Register_B__0_3), ._1_2(Register_B__1_2), ._2_2(Register_B__2_2), ._3_2(Register_B__3_2),
    ._4_2(Register_B__4_2), ._5_2(Register_B__5_2), ._6_2(Register_B__6_2), ._7_2(Register_B__7_2),
    .Clock(control_unit_1_acc_b_clock), .Reset(control_unit_1_ab_reset), ._0_2(Register_B__0_2));
  X x_1 (
    ._0_2(x_1__0_2), ._1_2(x_1__1_2), ._2_2(x_1__2_2), ._3_2(x_1__3_2), ._4_2(x_1__4_2), ._5_2(x_1__5_2),
    ._6_2(x_1__6_2), ._7_2(x_1__7_2), ._7(Register_B__0_3), ._6(Register_B__1_2), ._5(Register_B__2_2),
    ._4(Register_B__3_2), ._3(Register_B__4_2), ._2(Register_B__5_2), ._1(Register_B__6_2),
    ._0(Register_B__7_2));
  // Probe on Register_B__0_2
  ROM rom_2 (.addr(n8_bit_counter_1__0_2), .data(rom_2_data));  // open: sel
  assign controlled_buffer_1_out = _1 ? rom_2_data : 8'bz;  // Controlled_Buffer_part controlled_buffer_2
  Multiplexer #(.width(8)) multiplexer_1 (
    .in0({8{1'b0}}), .in1(controlled_buffer_1_out), .out(multiplexer_1_out),
    .sel(control_panel_1_enable_write));  // open: en
  and and_8 (and_8_out, n8_bit_counter_1__0_2[6], n8_bit_counter_1__0_2[7]);
  _3_Way_Multiplexor u_3_way_multiplexor_1 (
    ._0_2(Register_Y__0_3), ._1_2(Register_Y__1_2), ._2_2(Register_Y__2_2), ._3_2(Register_Y__3_2),
    ._4_2(Register_Y__4_2), ._5_2(Register_Y__5_2), ._6_2(Register_Y__6_2), ._7_2(Register_Y__7_2),
    ._0_3(x_1__7_2), ._1_3(x_1__6_2), ._2_3(x_1__5_2), ._3_3(x_1__4_2), ._4_3(x_1__3_2), ._5_3(x_1__2_2),
    ._6_3(x_1__1_2), ._7_3(x_1__0_2), ._7(MBR__7_2), ._6(MBR__6_2), ._5(MBR__5_2), ._4(MBR__4_2),
    ._3(MBR__3_2), ._2(MBR__2_2), ._1(MBR__1_2), ._0(MBR__0_3), ._7_4(n3_way_multiplexor_1__7_4),
    ._6_4(n3_way_multiplexor_1__6_4), ._5_4(n3_way_multiplexor_1__5_4), ._4_4(n3_way_multiplexor_1__4_4),
    ._3_4(n3_way_multiplexor_1__3_4), ._2_4(n3_way_multiplexor_1__2_4), ._1_4(n3_way_multiplexor_1__1_4),
    ._0_4(n3_way_multiplexor_1__0_4), .S0(control_unit_1_mp_alu_b_s0), .S1(control_unit_1_mp_alu_b_s1));
  _8_bit_Counter u_8_bit_counter_1 (
    .Increment(and_1_out), .Set(control_panel_1_program_reset_out), ._7_2(n8_bit_counter_1__0_2[7]),
    ._6_2(n8_bit_counter_1__0_2[6]), ._5_2(n8_bit_counter_1__0_2[5]), ._4_2(n8_bit_counter_1__0_2[4]),
    ._3_2(n8_bit_counter_1__0_2[3]), ._2_2(n8_bit_counter_1__0_2[2]), ._1_2(n8_bit_counter_1__0_2[1]),
    ._0_2(n8_bit_counter_1__0_2[0]), ._7(1'b0), ._6(1'b0), ._5(1'b0), ._4(1'b0), ._3(1'b0), ._2(1'b0),
    ._1(1'b0), ._0(1'b0));  // open: Increment_Out, Set_Carry
  _2_Way_Multiplexor u_2_way_multiplexor_1 (
    ._0(MAR__0_3), ._1(MAR__1_2), ._2(MAR__2_2), ._3(MAR__3_2), ._4(MAR__4_2), ._5(MAR__5_2), ._6(MAR__6_2),
    ._7(MAR__7_2), ._0_2(n8_bit_counter_1__0_2[0]), ._1_2(n8_bit_counter_1__0_2[1]),
    ._2_2(n8_bit_counter_1__0_2[2]), ._3_2(n8_bit_counter_1__0_2[3]), ._4_2(n8_bit_counter_1__0_2[4]),
    ._5_2(n8_bit_counter_1__0_2[5]), ._6_2(n8_bit_counter_1__0_2[6]), ._7_2(n8_bit_counter_1__0_2[7]),
    .S(control_panel_1_enable_write), ._0_3(n2_way_multiplexor_1__0_3[0]),
    ._1_3(n2_way_multiplexor_1__0_3[1]), ._2_3(n2_way_multiplexor_1__0_3[2]),
    ._3_3(n2_way_multiplexor_1__0_3[3]), ._4_3(n2_way_multiplexor_1__0_3[4]),
    ._5_3(n2_way_multiplexor_1__0_3[5]), ._6_3(n2_way_multiplexor_1__0_3[6]),
    ._7_3(n2_way_multiplexor_1__0_3[7]));
  _8_bit_Register MBR (
    ._7(ram_1_data[7]), ._6(ram_1_data[6]), ._5(ram_1_data[5]), ._4(ram_1_data[4]), ._3(ram_1_data[3]),
    ._2(ram_1_data[2]), ._1(ram_1_data[1]), ._0(ram_1_data[0]), ._0_3(MBR__0_3), ._1_2(MBR__1_2),
    ._2_2(MBR__2_2), ._3_2(MBR__3_2), ._4_2(MBR__4_2), ._5_2(MBR__5_2), ._6_2(MBR__6_2), ._7_2(MBR__7_2),
    .Clock(control_unit_1_mbr_clock), .Reset(control_unit_1_mbr_reset), ._0_2(MBR__0_2));
  // Probe on MBR__0_2
  _3_Way_Multiplexor u_3_way_multiplexor_2 (
    ._0_2(Register_A__0_3), ._1_2(Register_A__1_2), ._2_2(Register_A__2_2), ._3_2(Register_A__3_2),
    ._4_2(Register_A__4_2), ._5_2(Register_A__5_2), ._6_2(Register_A__6_2), ._7_2(Register_A__7_2),
    ._0_3(keyboard_1_data[0]), ._1_3(keyboard_1_data[1]), ._2_3(keyboard_1_data[2]),
    ._3_3(keyboard_1_data[3]), ._4_3(keyboard_1_data[4]), ._5_3(keyboard_1_data[5]),
    ._6_3(keyboard_1_data[6]), ._7_3(1'b0), ._7(Register_X__7_2), ._6(Register_X__6_2), ._5(Register_X__5_2),
    ._4(Register_X__4_2), ._3(Register_X__3_2), ._2(Register_X__2_2), ._1(Register_X__1_2),
    ._0(Register_X__0_3), ._7_4(n3_way_multiplexor_2__7_4), ._6_4(n3_way_multiplexor_2__6_4),
    ._5_4(n3_way_multiplexor_2__5_4), ._4_4(n3_way_multiplexor_2__4_4), ._3_4(n3_way_multiplexor_2__3_4),
    ._2_4(n3_way_multiplexor_2__2_4), ._1_4(n3_way_multiplexor_2__1_4), ._0_4(n3_way_multiplexor_2__0_4),
    .S0(control_unit_1_mp_alu_a_s0), .S1(control_unit_1_mp_alu_a_s1));
  ROM rom_3 (.addr(n8_bit_counter_1__0_2), .data(rom_3_data));  // open: sel
  assign controlled_buffer_1_out = _2 ? rom_3_data : 8'bz;  // Controlled_Buffer_part controlled_buffer_3
  ROM rom_4 (.addr(n8_bit_counter_1__0_2), .data(rom_4_data));  // open: sel
  assign controlled_buffer_1_out = _3 ? rom_4_data : 8'bz;  // Controlled_Buffer_part controlled_buffer_4
  // Probe on Register_Y__0_2
  _8_bit_Register Register_Y (
    ._7(Accumulator__7_2), ._6(Accumulator__0_3[6]), ._5(Accumulator__0_3[5]), ._4(Accumulator__0_3[4]),
    ._3(Accumulator__0_3[3]), ._2(Accumulator__0_3[2]), ._1(Accumulator__0_3[1]), ._0(Accumulator__0_3[0]),
    ._0_3(Register_Y__0_3), ._1_2(Register_Y__1_2), ._2_2(Register_Y__2_2), ._3_2(Register_Y__3_2),
    ._4_2(Register_Y__4_2), ._5_2(Register_Y__5_2), ._6_2(Register_Y__6_2), ._7_2(Register_Y__7_2),
    .Clock(control_unit_1_acc_y_clock), .Reset(control_unit_1_ay_reset), ._0_2(Register_Y__0_2));
  LED led_1 (.in(control_panel_1_system_clock));
  Control_Panel control_panel_1 (
    .Program_Reset_Out(control_panel_1_program_reset_out), .Write_Next_Byte(control_panel_1_write_next_byte),
    .Pregram_Reset(Program_Reset_out), .Write_Byte(Write_Byte_out),
    .Enable_Program_Write(Enable_Program_Write), .Reset(Reset_out), .Enable_Auto_Clock(Auto_Clock),
    .Tick(Tick_out), .One_by_One(One_by_One), .Reset_Out(control_panel_1_reset_out),
    .Clock(control_panel_1_clock), .One_by_One_2(control_panel_1_one_by_one_2),
    .Enable_Write(control_panel_1_enable_write), .Next_Instruction_2(control_panel_1_next_instruction_2),
    .Next_Instruction(Next_Instruction_out), .System_Clock(control_panel_1_system_clock));
  _3_Way_Multiplexor u_3_way_multiplexor_3 (
    ._0_2(x_2__0_2), ._1_2(x_2__1_2), ._2_2(x_2__2_2), ._3_2(x_2__3_2), ._4_2(x_2__4_2), ._5_2(x_2__5_2),
    ._6_2(x_2__6_2), ._7_2(x_2__7_2), ._0_3(multiplexer_1_out[0]), ._1_3(multiplexer_1_out[1]),
    ._2_3(multiplexer_1_out[2]), ._3_3(multiplexer_1_out[3]), ._4_3(multiplexer_1_out[4]),
    ._5_3(multiplexer_1_out[5]), ._6_3(multiplexer_1_out[6]), ._7_3(multiplexer_1_out[7]),
    ._7_4(n3_way_multiplexor_3__0_4[7]), ._6_4(n3_way_multiplexor_3__0_4[6]),
    ._5_4(n3_way_multiplexor_3__0_4[5]), ._4_4(n3_way_multiplexor_3__0_4[4]),
    ._3_4(n3_way_multiplexor_3__0_4[3]), ._2_4(n3_way_multiplexor_3__0_4[2]),
    ._1_4(n3_way_multiplexor_3__0_4[1]), ._0_4(n3_way_multiplexor_3__0_4[0]), .S0(1'b1),
    .S1(control_panel_1_enable_write));  // open: _7, _6, _5, _4, _3, _2, _1, _0
  Control_Unit control_unit_1 (
    .MP_ALU_A_S0(control_unit_1_mp_alu_a_s0), .MP_ALU_A_S1(control_unit_1_mp_alu_a_s1),
    .MP_ALU_B_S0(control_unit_1_mp_alu_b_s0), .MP_ALU_B_S1(control_unit_1_mp_alu_b_s1),
    .MAR_Clock(control_unit_1_mar_clock), .MBR_Clock(control_unit_1_mbr_clock),
    .Acc_X_Clock(control_unit_1_acc_x_clock), .Acc_A_Clock(control_unit_1_acc_a_clock),
    .Acc_B_Clock(control_unit_1_acc_b_clock), .Acc_Y_Clock(control_unit_1_acc_y_clock),
    .A_Clock(control_unit_1_a_clock), .MAR_Reset(control_unit_1_mar_reset),
    .MBR_Reset(control_unit_1_mbr_reset), .AX_Reset(control_unit_1_ax_reset),
    .AA_Reset(control_unit_1_aa_reset), .AB_Reset(control_unit_1_ab_reset),
    .AY_Reset(control_unit_1_ay_reset), .A_Reset(control_unit_1_a_reset), .Clock(control_panel_1_clock),
    .PC_Set(control_unit_1_pc_set), .PC_Count(control_unit_1_pc_count),
    .Not_Equal(condition_code_register_1_not_equal_2), .B_Greater_A(condition_code_register_1_b_greater_a_2),
    .A_Greater_B(condition_code_register_1_a_greater_b_2), .Carry_Out(condition_code_register_1_overflow_2),
    .Nero(undriven), .Negative(undriven_2), .Clock_B_Greater_A(control_unit_1_clock_b_greater_a),
    .Clock_CCR(control_unit_1_clock_ccr), .M_Clock(control_unit_1_m_clock),
    .MP_MAR_S1(control_unit_1_mp_mar_s1), .MP_MAR_S0(control_unit_1_mp_mar_s0),
    .MP_PC_S0(control_unit_1_mp_pc_s0), .IR_Reset(control_unit_1_ir_reset),
    .IR_Clock(control_unit_1_ir_clock), ._7(IR__7_2), ._6(IR__6_2), ._5(IR__5_2), ._4(IR__4_2), ._3(IR__3_2),
    ._2(IR__2_2), ._1(IR__1_2), ._0(IR__0_3), .A_Invert(control_unit_1_a_invert),
    .B_Invert(control_unit_1_b_invert), .AND(control_unit_1_and), .OR(control_unit_1_or),
    .A(control_unit_1_a), .B(control_unit_1_b), .Shift_A_Right(control_unit_1_shift_a_right),
    .Shift_B_Right(control_unit_1_shift_b_right), .Shift_Loop(control_unit_1_shift_loop),
    .Shift_A_Left(control_unit_1_shift_a_left), .Shift_B_Left(control_unit_1_shift_b_left),
    .XOR(control_unit_1_xor), .Increment(control_unit_1_increment), .ADD(control_unit_1_add),
    .X_Invert(control_unit_1_x_invert), .Reset(control_panel_1_reset_out),
    .MP_PC_S1(control_unit_1_mp_pc_s1), .Stack_Pop(control_unit_1_stack_pop),
    .Stack_Push(control_unit_1_stack_push), .Stack_Reset(control_unit_1_stack_reset),
    .Display_Clock(control_unit_1_display_clock), .MP_MAR_S2(control_unit_1_mp_mar_s2),
    .Read_Input(control_unit_1_read_input), .Input_Available(keyboard_1_avail),
    .Reset_IO(control_unit_1_reset_io), .Next_Instruction(control_panel_1_next_instruction_2),
    .One_by_One(control_panel_1_one_by_one_2), .Set_MAR_Add_MBR(control_unit_1_set_mar_add_mbr),
    .Multiply(control_unit_1_multiply));  // open: Set_Carry_Selector, Set_Carry_Data
  ALU alu_1 (
    .A0(n3_way_multiplexor_2__0_4), .B0(n3_way_multiplexor_1__0_4), .A1(n3_way_multiplexor_2__1_4),
    .B1(n3_way_multiplexor_1__1_4), .A2(n3_way_multiplexor_2__2_4), .B2(n3_way_multiplexor_1__2_4),
    .A3(n3_way_multiplexor_2__3_4), .B3(n3_way_multiplexor_1__3_4), .A4(n3_way_multiplexor_2__4_4),
    .B4(n3_way_multiplexor_1__4_4), .A5(n3_way_multiplexor_2__5_4), .B5(n3_way_multiplexor_1__5_4),
    .A6(n3_way_multiplexor_2__6_4), .B6(n3_way_multiplexor_1__6_4), .A7(n3_way_multiplexor_2__7_4),
    .B7(n3_way_multiplexor_1__7_4), .X0(alu_1_x0), .X1(alu_1_x1), .X2(alu_1_x2), .X3(alu_1_x3),
    .X4(alu_1_x4), .X5(alu_1_x5), .X6(alu_1_x6), .X7(alu_1_x7), .A_Invert(control_unit_1_a_invert),
    .B_Invert(control_unit_1_b_invert), .AND(control_unit_1_and), .OR(control_unit_1_or),
    .A(control_unit_1_a), .B(control_unit_1_b), .Shift_A_Right(control_unit_1_shift_a_right),
    .Shift_B_Right(control_unit_1_shift_b_right), .Shift_A_Left(control_unit_1_shift_a_left),
    .Shift_B_Left(control_unit_1_shift_b_left), .XOR(control_unit_1_xor),
    .Increment(control_unit_1_increment), .ADD(control_unit_1_add), .X_Invert(control_unit_1_x_invert),
    .Not_Equal(alu_1_not_equal), .B_Greater_A(alu_1_b_greater_a), .A_Greater_B(alu_1_a_greater_b),
    .Overflow(alu_1_overflow), .Shift_Loop(control_unit_1_shift_loop), .Zero(alu_1_zero),
    .Multiply(control_unit_1_multiply));
  Button Program_Reset (.out(Program_Reset_out));
  Button Write_Byte (.out(Write_Byte_out));
  Button Reset (.out(Reset_out));
  Button Tick (.out(Tick_out));
  Button Next_Instruction (.out(Next_Instruction_out));
  // Probe on MAR__0_2
  _8_bit_Register MAR (
    ._7(n8_bit_adder_1_x7), ._6(n8_bit_adder_1_x6), ._5(n8_bit_adder_1_x5), ._4(n8_bit_adder_1_x4),
    ._3(n8_bit_adder_1_x3), ._2(n8_bit_adder_1_x2), ._1(n8_bit_adder_1_x1), ._0(n8_bit_adder_1_x0),
    ._0_3(MAR__0_3), ._1_2(MAR__1_2), ._2_2(MAR__2_2), ._3_2(MAR__3_2), ._4_2(MAR__4_2), ._5_2(MAR__5_2),
    ._6_2(MAR__6_2), ._7_2(MAR__7_2), .Clock(control_unit_1_mar_clock), .Reset(control_unit_1_mar_reset),
    ._0_2(MAR__0_2));
  X x_2 (
    ._0_2(x_2__0_2), ._1_2(x_2__1_2), ._2_2(x_2__2_2), ._3_2(x_2__3_2), ._4_2(x_2__4_2), ._5_2(x_2__5_2),
    ._6_2(x_2__6_2), ._7_2(x_2__7_2), ._7(Accumulator__7_2), ._6(Accumulator__0_3[6]),
    ._5(Accumulator__0_3[5]), ._4(Accumulator__0_3[4]), ._3(Accumulator__0_3[3]), ._2(Accumulator__0_3[2]),
    ._1(Accumulator__0_3[1]), ._0(Accumulator__0_3[0]));
  _8_bit_Register Accumulator (
    ._7(alu_1_x7), ._6(alu_1_x6), ._5(alu_1_x5), ._4(alu_1_x4), ._3(alu_1_x3), ._2(alu_1_x2), ._1(alu_1_x1),
    ._0(alu_1_x0), ._0_3(Accumulator__0_3[0]), ._1_2(Accumulator__0_3[1]), ._2_2(Accumulator__0_3[2]),
    ._3_2(Accumulator__0_3[3]), ._4_2(Accumulator__0_3[4]), ._5_2(Accumulator__0_3[5]),
    ._6_2(Accumulator__0_3[6]), ._7_2(Accumulator__7_2), .Clock(control_unit_1_a_clock),
    .Reset(control_unit_1_a_reset), ._0_2(Accumulator__0_2));
  // Probe on Accumulator__0_2
  TTY #(.rows(10)) tty_1 (.data(Accumulator__0_3), .clk(control_unit_1_display_clock), .clr(or_2_out));  // open: we
  or or_2 (or_2_out, and_9_out, control_unit_1_reset_io);
  Keyboard keyboard_1 (
    .clk(control_unit_1_read_input), .clr(or_3_out), .avail(keyboard_1_avail), .data(keyboard_1_data));  // open: re
  and and_9 (and_9_out, control_unit_1_display_clock, Accumulator__7_2);
  _8_bit_Adder u_8_bit_adder_1 (
    .A0(x_3__0_2), .B0(controlled_buffer_5_x0), .A1(x_3__1_2), .B1(controlled_buffer_5_x1), .A2(x_3__2_2),
    .B2(controlled_buffer_5_x2), .A3(x_3__3_2), .B3(controlled_buffer_5_x3), .A4(x_3__4_2),
    .B4(controlled_buffer_5_x4), .A5(x_3__5_2), .B5(controlled_buffer_5_x5), .A6(x_3__6_2),
    .B6(controlled_buffer_5_x6), .A7(x_3__7_2), .B7(controlled_buffer_5_x7), .X0(n8_bit_adder_1_x0),
    .X1(n8_bit_adder_1_x1), .X2(n8_bit_adder_1_x2), .X3(n8_bit_adder_1_x3), .X4(n8_bit_adder_1_x4),
    .X5(n8_bit_adder_1_x5), .X6(n8_bit_adder_1_x6), .X7(n8_bit_adder_1_x7), .Increment(1'b0));  // open: Carry_Out
  X x_3 (
    ._0_2(x_3__0_2), ._1_2(x_3__1_2), ._2_2(x_3__2_2), ._3_2(x_3__3_2), ._4_2(x_3__4_2), ._5_2(x_3__5_2),
    ._6_2(x_3__6_2), ._7_2(x_3__7_2), ._7(n5_way_multiplexer_1__7_6), ._6(n5_way_multiplexer_1__6_6),
    ._5(n5_way_multiplexer_1__5_6), ._4(n5_way_multiplexer_1__4_6), ._3(n5_way_multiplexer_1__3_6),
    ._2(n5_way_multiplexer_1__2_6), ._1(n5_way_multiplexer_1__1_6), ._0(n5_way_multiplexer_1__0_6));
  _5_Way_Multiplexer u_5_way_multiplexer_1 (
    ._0(Accumulator__0_3[0]), ._1(Accumulator__0_3[1]), ._2(Accumulator__0_3[2]), ._3(Accumulator__0_3[3]),
    ._4(Accumulator__0_3[4]), ._5(Accumulator__0_3[5]), ._6(Accumulator__0_3[6]), ._7(Accumulator__7_2),
    ._0_3(Register_X__0_3), ._1_3(Register_X__1_2), ._2_3(Register_X__2_2), ._3_3(Register_X__3_2),
    ._4_3(Register_X__4_2), ._5_3(Register_X__5_2), ._6_3(Register_X__6_2), ._7_3(Register_X__7_2),
    ._0_2(PC__0_2), ._1_2(PC__1_2), ._2_2(PC__2_2), ._3_2(PC__3_2), ._4_2(PC__4_2), ._5_2(PC__5_2),
    ._6_2(PC__6_2), ._7_2(PC__7_2), ._0_4(Register_Y__0_3), ._1_4(Register_Y__1_2), ._2_4(Register_Y__2_2),
    ._3_4(Register_Y__3_2), ._4_4(Register_Y__4_2), ._5_4(Register_Y__5_2), ._6_4(Register_Y__6_2),
    ._7_4(Register_Y__7_2), ._7_6(n5_way_multiplexer_1__7_6), ._6_6(n5_way_multiplexer_1__6_6),
    ._5_6(n5_way_multiplexer_1__5_6), ._4_6(n5_way_multiplexer_1__4_6), ._3_6(n5_way_multiplexer_1__3_6),
    ._2_6(n5_way_multiplexer_1__2_6), ._1_6(n5_way_multiplexer_1__1_6), ._0_6(n5_way_multiplexer_1__0_6),
    ._7_5(x_4__0_2), ._6_5(x_4__1_2), ._5_5(x_4__2_2), ._4_5(x_4__3_2), ._3_5(x_4__4_2), ._2_5(x_4__5_2),
    ._1_5(x_4__6_2), ._0_5(x_4__7_2), .S2(control_unit_1_mp_mar_s2), .S1(control_unit_1_mp_mar_s1),
    .S0(control_unit_1_mp_mar_s0));
  X x_4 (
    ._0_2(x_4__0_2), ._1_2(x_4__1_2), ._2_2(x_4__2_2), ._3_2(x_4__3_2), ._4_2(x_4__4_2), ._5_2(x_4__5_2),
    ._6_2(x_4__6_2), ._7_2(x_4__7_2), ._7(MBR__0_3), ._6(MBR__1_2), ._5(MBR__2_2), ._4(MBR__3_2),
    ._3(MBR__4_2), ._2(MBR__5_2), ._1(MBR__6_2), ._0(MBR__7_2));
  or or_3 (or_3_out, control_unit_1_reset_io, Clear_Input_out);
  Controlled_Buffer controlled_buffer_5 (
    .Control(control_unit_1_set_mar_add_mbr), .X7(controlled_buffer_5_x7), .X6(controlled_buffer_5_x6),
    .X5(controlled_buffer_5_x5), .X4(controlled_buffer_5_x4), .X3(controlled_buffer_5_x3),
    .X2(controlled_buffer_5_x2), .X1(controlled_buffer_5_x1), .X0(controlled_buffer_5_x0), .A7(MBR__7_2),
    .A6(MBR__6_2), .A5(MBR__5_2), .A4(MBR__4_2), .A3(MBR__3_2), .A2(MBR__2_2), .A1(MBR__1_2), .A0(MBR__0_3));
  _8_bit_Register IR (
    ._7(MBR__7_2), ._6(MBR__6_2), ._5(MBR__5_2), ._4(MBR__4_2), ._3(MBR__3_2), ._2(MBR__2_2), ._1(MBR__1_2),
    ._0(MBR__0_3), ._0_3(IR__0_3), ._1_2(IR__1_2), ._2_2(IR__2_2), ._3_2(IR__3_2), ._4_2(IR__4_2),
    ._5_2(IR__5_2), ._6_2(IR__6_2), ._7_2(IR__7_2), .Clock(control_unit_1_ir_clock),
    .Reset(control_unit_1_ir_reset), ._0_2(IR__0_2));
  // Probe on IR__0_2
  LED led_2 (.in(condition_code_register_1_not_equal_2));
  Condition_Code_Register condition_code_register_1 (
    .Not_Equal(alu_1_not_equal), .B_Greater_A(alu_1_b_greater_a), .A_Greater_B(alu_1_a_greater_b),
    .Overflow(alu_1_overflow), .Zero(alu_1_zero), .Negative(Accumulator__7_2),
    .Not_Equal_2(condition_code_register_1_not_equal_2),
    .B_Greater_A_2(condition_code_register_1_b_greater_a_2),
    .A_Greater_B_2(condition_code_register_1_a_greater_b_2),
    .Overflow_2(condition_code_register_1_overflow_2), .Zero_2(condition_code_register_1_zero_2),
    .Negative_2(condition_code_register_1_negative_2), .Waiting_2(condition_code_register_1_waiting_2),
    .Finished_2(condition_code_register_1_finished_2), .Clear_Finished(undriven_3), .Clear_Wait(undriven_4),
    .Clock(control_unit_1_clock_ccr));  // open: Waiting, Finished
  LED led_3 (.in(condition_code_register_1_b_greater_a_2));
  LED led_4 (.in(condition_code_register_1_a_greater_b_2));
  LED led_5 (.in(condition_code_register_1_overflow_2));
  LED led_6 (.in(condition_code_register_1_zero_2));
  LED led_7 (.in(condition_code_register_1_negative_2));
  LED led_8 (.in(condition_code_register_1_waiting_2));
  LED led_9 (.in(condition_code_register_1_finished_2));
  Button Clear_Input (.out(Clear_Input_out));
  // Probe on joystick_1_x
  Joystick joystick_1 (.x(joystick_1_x), .y(joystick_1_y));
  // Probe on joystick_1_y
  _3_Way_Multiplexor u_3_way_multiplexor_4 (
    ._0_2(Accumulator__7_2), ._1_2(Accumulator__0_3[6]), ._2_2(Accumulator__0_3[5]),
    ._3_2(Accumulator__0_3[4]), ._4_2(Accumulator__0_3[3]), ._5_2(Accumulator__0_3[2]),
    ._6_2(Accumulator__0_3[1]), ._7_2(Accumulator__0_3[0]), ._0_3(n8_bit_stack_1__0_2),
    ._1_3(n8_bit_stack_1__1_2), ._2_3(n8_bit_stack_1__2_2), ._3_3(n8_bit_stack_1__3_2),
    ._4_3(n8_bit_stack_1__4_2), ._5_3(n8_bit_stack_1__5_2), ._6_3(n8_bit_stack_1__6_2),
    ._7_3(n8_bit_stack_1__7_2), ._7(MBR__7_2), ._6(MBR__6_2), ._5(MBR__5_2), ._4(MBR__4_2), ._3(MBR__3_2),
    ._2(MBR__2_2), ._1(MBR__1_2), ._0(MBR__0_3), ._7_4(n3_way_multiplexor_4__7_4),
    ._6_4(n3_way_multiplexor_4__6_4), ._5_4(n3_way_multiplexor_4__5_4), ._4_4(n3_way_multiplexor_4__4_4),
    ._3_4(n3_way_multiplexor_4__3_4), ._2_4(n3_way_multiplexor_4__2_4), ._1_4(n3_way_multiplexor_4__1_4),
    ._0_4(n3_way_multiplexor_4__0_4), .S0(control_unit_1_mp_pc_s0), .S1(control_unit_1_mp_pc_s1));
  Hex_Digit_Display hex_digit_display_1 (.value(n8_bit_counter_2__4_2));  // open: dp
  _8_bit_Counter u_8_bit_counter_2 (
    .Increment(n8_bit_counter_3_increment_out), .Set(n8_bit_counter_3_set_carry),
    ._7_2(n8_bit_counter_2__4_2[3]), ._6_2(n8_bit_counter_2__4_2[2]), ._5_2(n8_bit_counter_2__4_2[1]),
    ._4_2(n8_bit_counter_2__4_2[0]), ._3_2(n8_bit_counter_2__0_2[3]), ._2_2(n8_bit_counter_2__0_2[2]),
    ._1_2(n8_bit_counter_2__0_2[1]), ._0_2(n8_bit_counter_2__0_2[0]), ._7(1'b0), ._6(1'b0), ._5(1'b0),
    ._4(1'b0), ._3(1'b0), ._2(1'b0), ._1(1'b0), ._0(1'b0));  // open: Increment_Out, Set_Carry
  Hex_Digit_Display hex_digit_display_2 (.value(n8_bit_counter_3__4_2));  // open: dp
  Hex_Digit_Display hex_digit_display_3 (.value(n8_bit_counter_2__0_2));  // open: dp
  _8_bit_Stack u_8_bit_stack_1 (
    ._0_2(n8_bit_stack_1__0_2), ._1_2(n8_bit_stack_1__1_2), ._2_2(n8_bit_stack_1__2_2),
    ._3_2(n8_bit_stack_1__3_2), ._4_2(n8_bit_stack_1__4_2), ._5_2(n8_bit_stack_1__5_2),
    ._6_2(n8_bit_stack_1__6_2), ._7_2(n8_bit_stack_1__7_2), .Reset(control_unit_1_stack_reset),
    .Push(control_unit_1_stack_push), .Pop(control_unit_1_stack_pop), ._7(PC__7_2), ._6(PC__6_2),
    ._5(PC__5_2), ._4(PC__4_2), ._3(PC__3_2), ._2(PC__2_2), ._1(PC__1_2), ._0(PC__0_2));
  _8_bit_Counter PC (
    .Increment(control_unit_1_pc_count), .Set(control_unit_1_pc_set), ._7_2(PC__7_2), ._6_2(PC__6_2),
    ._5_2(PC__5_2), ._4_2(PC__4_2), ._3_2(PC__3_2), ._2_2(PC__2_2), ._1_2(PC__1_2), ._0_2(PC__0_2),
    ._7(n3_way_multiplexor_4__7_4), ._6(n3_way_multiplexor_4__6_4), ._5(n3_way_multiplexor_4__5_4),
    ._4(n3_way_multiplexor_4__4_4), ._3(n3_way_multiplexor_4__3_4), ._2(n3_way_multiplexor_4__2_4),
    ._1(n3_way_multiplexor_4__1_4), ._0(n3_way_multiplexor_4__0_4));  // open: Increment_Out, Set_Carry
  Hex_Digit_Display hex_digit_display_4 (.value(n8_bit_counter_3__0_2));  // open: dp
  _8_bit_Counter u_8_bit_counter_3 (
    .Increment(n8_bit_counter_4_increment_out), .Set(n8_bit_counter_4_set_carry),
    ._7_2(n8_bit_counter_3__4_2[3]), ._6_2(n8_bit_counter_3__4_2[2]), ._5_2(n8_bit_counter_3__4_2[1]),
    ._4_2(n8_bit_counter_3__4_2[0]), ._3_2(n8_bit_counter_3__0_2[3]), ._2_2(n8_bit_counter_3__0_2[2]),
    ._1_2(n8_bit_counter_3__0_2[1]), ._0_2(n8_bit_counter_3__0_2[0]), ._7(1'b0), ._6(1'b0), ._5(1'b0),
    ._4(1'b0), ._3(1'b0), ._2(1'b0), ._1(1'b0), ._0(1'b0), .Increment_Out(n8_bit_counter_3_increment_out),
    .Set_Carry(n8_bit_counter_3_set_carry));
  Hex_Digit_Display hex_digit_display_5 (.value(n8_bit_counter_4__0_2));  // open: dp
  Hex_Digit_Display hex_digit_display_6 (.value(n8_bit_counter_4__4_2));  // open: dp
  _8_bit_Counter u_8_bit_counter_4 (
    .Increment(n8_bit_counter_5_increment_out), .Set(n8_bit_counter_5_set_carry),
    ._7_2(n8_bit_counter_4__4_2[3]), ._6_2(n8_bit_counter_4__4_2[2]), ._5_2(n8_bit_counter_4__4_2[1]),
    ._4_2(n8_bit_counter_4__4_2[0]), ._3_2(n8_bit_counter_4__0_2[3]), ._2_2(n8_bit_counter_4__0_2[2]),
    ._1_2(n8_bit_counter_4__0_2[1]), ._0_2(n8_bit_counter_4__0_2[0]), ._7(1'b0), ._6(1'b0), ._5(1'b0),
    ._4(1'b0), ._3(1'b0), ._2(1'b0), ._1(1'b0), ._0(1'b0), .Increment_Out(n8_bit_counter_4_increment_out),
    .Set_Carry(n8_bit_counter_4_set_carry));
  Hex_Digit_Display hex_digit_display_7 (.value(n8_bit_counter_5__0_2));  // open: dp
  Hex_Digit_Display hex_digit_display_8 (.value(n8_bit_counter_5__4_2));  // open: dp
  _8_bit_Counter u_8_bit_counter_5 (
    .Increment(control_panel_1_clock), ._7_2(n8_bit_counter_5__4_2[3]), ._6_2(n8_bit_counter_5__4_2[2]),
    ._5_2(n8_bit_counter_5__4_2[1]), ._4_2(n8_bit_counter_5__4_2[0]), ._3_2(n8_bit_counter_5__0_2[3]),
    ._2_2(n8_bit_counter_5__0_2[2]), ._1_2(n8_bit_counter_5__0_2[1]), ._0_2(n8_bit_counter_5__0_2[0]),
    ._7(1'b0), ._6(1'b0), ._5(1'b0), ._4(1'b0), ._3(1'b0), ._2(1'b0), ._1(1'b0), ._0(1'b0),
    .Increment_Out(n8_bit_counter_5_increment_out), .Set_Carry(n8_bit_counter_5_set_carry));  // open: Set
  LED_Matrix_Controller led_matrix_controller_1 (
    .Value(in_8), .Clear(in_9), .Clock(in_10), .out_12(led_matrix_controller_1_out_12),
    .out_13(led_matrix_controller_1_out_13), .out_14(led_matrix_controller_1_out_14),
    .out_15(led_matrix_controller_1_out_15), .out_16(led_matrix_controller_1_out_16),
    .out_17(led_matrix_controller_1_out_17), .out_18(led_matrix_controller_1_out_18),
    .out_19(led_matrix_controller_1_out_19), .out_20(led_matrix_controller_1_out_20),
    .out_21(led_matrix_controller_1_out_21), .out_22(led_matrix_controller_1_out_22),
    .out_23(led_matrix_controller_1_out_23), .out_24(led_matrix_controller_1_out_24),
    .out_25(led_matrix_controller_1_out_25), .out_26(led_matrix_controller_1_out_26),
    .out_27(led_matrix_controller_1_out_27), .in_4(in_11), .in_5(in_12), .in_6(in_13), .in_7(in_14),
    .in_8(in_15), .in_9(in_16), .in_10(in_17), .in_11(in_18));
  DotMatrix #(.inputtype("row"), .matrixcols(16), .matrixrows(16)) dotmatrix_1 (
    .row0(led_matrix_controller_1_out_12), .row1(led_matrix_controller_1_out_13),
    .row2(led_matrix_controller_1_out_14), .row3(led_matrix_controller_1_out_15),
    .row4(led_matrix_controller_1_out_16), .row5(led_matrix_controller_1_out_17),
    .row6(led_matrix_controller_1_out_18), .row7(led_matrix_controller_1_out_19),
    .row8(led_matrix_controller_1_out_20), .row9(led_matrix_controller_1_out_21),
    .row10(led_matrix_controller_1_out_22), .row11(led_matrix_controller_1_out_23),
    .row12(led_matrix_controller_1_out_24), .row13(led_matrix_controller_1_out_25),
    .row14(led_matrix_controller_1_out_26), .row15(led_matrix_controller_1_out_27));

  // Notes on the sheet:
  //   Program 0
  //   contents of rom_1 (hex, n*v repeats v):
  //   36 0 3a 0 34 15 6f 78 d 4e 26 75 4 52 a 58 56 4e 75 f 3 48 65 6c 6c 6f 20 57 6f 72 6c 64 21 20 3a 29
  //   Program 1
  //   contents of rom_2 (hex, n*v repeats v):
  //   58 56 4e 20 46 71 a 7a b 20 47 59 52 20 52 2b 52 20 58 56 4e 20 46 71 a 7a 1d 20 47 10 52 20 52 3d
  //   52 20 5d 36 f0 3e f 8c 8f 4*65 19 46 71 39 7c 37 19 47 4e 5e 19 46 71 39 7c 41 19 47 4e 52 a 75 0 30
  //   7 0 0 1 8
  //   Program 2
  //   contents of rom_3 (hex, n*v repeats v):
  //   58 56 4e 20 46 71 a 7a b 20 47 59 52 20 52 78 52 20 58 56 4e 20 46 71 a 7a 1d 20 47 4 52 20 52 3d 52
  //   20 5d 36 f0 3e f 8c 8f 4*65 19 46 71 39 7c 37 19 47 4e 5e 19 46 71 39 7c 41 19 47 4e 52 a 75 0 30 7
  //   0 0 1 8
  //   Program 3
  //   contents of rom_4 (hex, n*v repeats v):
  //   37 0 3b 0 35 22 70 79 d 4f 27 76 4 53 a 1 1b 53 58 53 a 59 57 4f 76 15 4 53 46 53 75 53 6e 3 48 65
  //   6c 6c 6f 20 57 6f 72 6c 64 21 20 3a 29
endmodule

module _1_bit_ALU (
  input  SLAI,
  input  SLBI,
  input  Carry_in,
  input  A_invert,
  input  B_invert,
  input  And,
  input  Or,
  input  A,
  input  B,
  input  SRA,
  input  SRB,
  input  SLA,
  input  SLB,
  input  XOr,
  input  Add,
  input  X_invert,
  input  Not_Zero_In,
  input  A_2,
  input  B_2,
  input  NEI,
  input  GRI,
  input  LSI,
  input  SRAI,
  input  SRBI,
  output SRAO,
  output SRBO,
  output NEO,
  output GRO,
  output LSO,
  output X,
  output out_31,
  output out_32,
  output out_33,
  output out_34,
  output out_35,
  output out_36,
  output out_37,
  output out_38,
  output out_39,
  output out_40,
  output out_41,
  output Carry_out,
  output out_43,
  output out_44,
  output Not_Zero_Out,
  output SLAO,
  output SLBO
);

  wire and_1_out, and_2_out, and_5_out, and_6_out, and_7_out, and_8_out, and_9_out, and_10_out, and_11_out,
       and_12_out, and_13_out, and_14_out, and_15_out, and_16_out, and_17_out, and_18_out, and_19_out,
       and_20_out, and_21_out, and_22_out, and_23_out, and_24_out, and_25_out, and_26_out, not_1_out,
       not_2_out, not_3_out, not_4_out, not_5_out, not_6_out, not_7_out, not_8_out, not_9_out, not_10_out,
       or_1_out, or_2_out, or_3_out, or_4_out, or_5_out, or_6_out, or_7_out, or_8_out, or_9_out, or_10_out,
       or_12_out, or_13_out, or_16_out, or_18_out, or_19_out, or_20_out;

  or or_1 (or_1_out, A_invert, A_2);
  and and_1 (and_1_out, A_invert, A_2);
  and and_2 (and_2_out, B_2, B_invert);
  or or_2 (or_2_out, B_2, B_invert);
  and and_3 (SLAO, or_1_out, not_1_out);
  not not_1 (not_1_out, and_1_out);
  not not_2 (not_2_out, and_2_out);
  and and_4 (SLBO, not_2_out, or_2_out);
  and and_5 (and_5_out, SLBO, SLAO);
  or or_3 (or_3_out, SLBO, SLAO);
  and and_6 (and_6_out, and_5_out, And);
  and and_7 (and_7_out, or_3_out, Or);
  and and_8 (and_8_out, SLAO, A);
  or or_4 (or_4_out, and_7_out, and_6_out);
  and and_9 (and_9_out, SLBO, B);
  or or_5 (or_5_out, and_9_out, or_6_out);
  or or_6 (or_6_out, and_8_out, or_4_out);
  and and_10 (and_10_out, SRAI, SRA);
  and and_11 (and_11_out, SRBI, SRB);
  or or_7 (or_7_out, and_10_out, or_5_out);
  or or_8 (or_8_out, or_7_out, and_11_out);
  and and_12 (and_12_out, SLBI, SLB);
  or or_9 (or_9_out, and_12_out, and_13_out);
  and and_13 (and_13_out, SLAI, SLA);
  or or_10 (or_10_out, SLAO, SLBO);
  not not_3 (not_3_out, and_14_out);
  and and_14 (and_14_out, SLAO, SLBO);
  and and_15 (and_15_out, or_10_out, not_3_out);
  or or_11 (NEO, and_15_out, NEI);
  and and_16 (and_16_out, and_15_out, XOr);
  or or_12 (or_12_out, and_16_out, or_8_out);
  not not_4 (not_4_out, SLAO);
  and and_17 (and_17_out, not_4_out, SLBO);
  or or_13 (or_13_out, or_9_out, or_12_out);
  or or_14 (GRO, and_18_out, GRI);
  and and_18 (and_18_out, and_17_out, not_5_out);
  not not_5 (not_5_out, LSI);
  not not_6 (not_6_out, GRI);
  not not_7 (not_7_out, SLBO);
  or or_15 (LSO, and_19_out, LSI);
  and and_19 (and_19_out, not_6_out, and_20_out);
  and and_20 (and_20_out, SLAO, not_7_out);
  or or_16 (or_16_out, SLAO, SLBO);
  and and_21 (and_21_out, SLAO, SLBO);
  and and_22 (and_22_out, or_16_out, not_8_out);
  not not_8 (not_8_out, and_21_out);
  or or_17 (Carry_out, and_21_out, and_23_out);
  or or_18 (or_18_out, and_22_out, Carry_in);
  and and_23 (and_23_out, and_22_out, Carry_in);
  not not_9 (not_9_out, and_23_out);
  and and_24 (and_24_out, or_18_out, not_9_out);
  and and_25 (and_25_out, and_24_out, Add);
  or or_19 (or_19_out, and_25_out, or_13_out);
  or or_20 (or_20_out, X_invert, or_19_out);
  not not_10 (not_10_out, and_26_out);
  and and_26 (and_26_out, X_invert, or_19_out);
  and and_27 (X, or_20_out, not_10_out);
  or or_21 (Not_Zero_Out, X, Not_Zero_In);

  assign out_31 = A_invert;
  assign out_32 = B_invert;
  assign out_33 = And;
  assign out_34 = Or;
  assign out_35 = A;
  assign out_36 = B;
  assign out_37 = SRA;
  assign out_38 = SRB;
  assign out_39 = SLA;
  assign out_40 = SLB;
  assign out_41 = XOr;
  assign out_43 = Add;
  assign out_44 = X_invert;
  assign SRAO = SLAO;
  assign SRBO = SLBO;
endmodule

module ALU (
  input  A_Invert,
  input  B_Invert,
  input  AND,
  input  OR,
  input  A,
  input  B,
  input  Shift_A_Right,
  input  Shift_B_Right,
  input  Shift_Loop,
  input  Shift_A_Left,
  input  Shift_B_Left,
  input  XOR,
  input  Increment,
  input  ADD,
  input  X_Invert,
  input  Multiply,
  input  A0,
  input  A1,
  input  A2,
  input  A3,
  input  A4,
  input  A5,
  input  A6,
  input  A7,
  input  B0,
  input  B1,
  input  B2,
  input  B3,
  input  B4,
  input  B5,
  input  B6,
  input  B7,
  output Not_Equal,
  output B_Greater_A,
  output A_Greater_B,
  output X0,
  output X1,
  output X2,
  output X3,
  output X4,
  output X5,
  output X6,
  output X7,
  output Zero,
  output Overflow
);

  wire and_1_out, and_2_out, and_3_out, and_4_out, n1_bit_alu_1_carry_out, n1_bit_alu_1_not_zero_out,
       n1_bit_alu_1_out_31, n1_bit_alu_1_out_32, n1_bit_alu_1_out_33, n1_bit_alu_1_out_34,
       n1_bit_alu_1_out_35, n1_bit_alu_1_out_36, n1_bit_alu_1_out_37, n1_bit_alu_1_out_38,
       n1_bit_alu_1_out_39, n1_bit_alu_1_out_40, n1_bit_alu_1_out_41, n1_bit_alu_1_out_43,
       n1_bit_alu_1_out_44, n1_bit_alu_1_slao, n1_bit_alu_1_slbo, n1_bit_alu_1_srao, n1_bit_alu_1_srbo,
       n1_bit_alu_1_x, n1_bit_alu_2_carry_out, n1_bit_alu_2_gro, n1_bit_alu_2_lso, n1_bit_alu_2_neo,
       n1_bit_alu_2_not_zero_out, n1_bit_alu_2_out_31, n1_bit_alu_2_out_32, n1_bit_alu_2_out_33,
       n1_bit_alu_2_out_34, n1_bit_alu_2_out_35, n1_bit_alu_2_out_36, n1_bit_alu_2_out_37,
       n1_bit_alu_2_out_38, n1_bit_alu_2_out_39, n1_bit_alu_2_out_40, n1_bit_alu_2_out_41,
       n1_bit_alu_2_out_43, n1_bit_alu_2_out_44, n1_bit_alu_2_slao, n1_bit_alu_2_slbo, n1_bit_alu_2_srao,
       n1_bit_alu_2_srbo, n1_bit_alu_2_x, n1_bit_alu_3_carry_out, n1_bit_alu_3_gro, n1_bit_alu_3_lso,
       n1_bit_alu_3_neo, n1_bit_alu_3_not_zero_out, n1_bit_alu_3_out_31, n1_bit_alu_3_out_32,
       n1_bit_alu_3_out_33, n1_bit_alu_3_out_34, n1_bit_alu_3_out_35, n1_bit_alu_3_out_36,
       n1_bit_alu_3_out_37, n1_bit_alu_3_out_38, n1_bit_alu_3_out_39, n1_bit_alu_3_out_40,
       n1_bit_alu_3_out_41, n1_bit_alu_3_out_43, n1_bit_alu_3_out_44, n1_bit_alu_3_slao, n1_bit_alu_3_slbo,
       n1_bit_alu_3_srao, n1_bit_alu_3_srbo, n1_bit_alu_3_x, n1_bit_alu_4_carry_out, n1_bit_alu_4_gro,
       n1_bit_alu_4_lso, n1_bit_alu_4_neo, n1_bit_alu_4_not_zero_out, n1_bit_alu_4_out_31,
       n1_bit_alu_4_out_32, n1_bit_alu_4_out_33, n1_bit_alu_4_out_34, n1_bit_alu_4_out_35,
       n1_bit_alu_4_out_36, n1_bit_alu_4_out_37, n1_bit_alu_4_out_38, n1_bit_alu_4_out_39,
       n1_bit_alu_4_out_40, n1_bit_alu_4_out_41, n1_bit_alu_4_out_43, n1_bit_alu_4_out_44, n1_bit_alu_4_slao,
       n1_bit_alu_4_slbo, n1_bit_alu_4_srao, n1_bit_alu_4_srbo, n1_bit_alu_4_x, n1_bit_alu_5_carry_out,
       n1_bit_alu_5_gro, n1_bit_alu_5_lso, n1_bit_alu_5_neo, n1_bit_alu_5_not_zero_out, n1_bit_alu_5_out_31,
       n1_bit_alu_5_out_32, n1_bit_alu_5_out_33, n1_bit_alu_5_out_34, n1_bit_alu_5_out_35,
       n1_bit_alu_5_out_36, n1_bit_alu_5_out_37, n1_bit_alu_5_out_38, n1_bit_alu_5_out_39,
       n1_bit_alu_5_out_40, n1_bit_alu_5_out_41, n1_bit_alu_5_out_43, n1_bit_alu_5_out_44, n1_bit_alu_5_slao,
       n1_bit_alu_5_slbo, n1_bit_alu_5_srao, n1_bit_alu_5_srbo, n1_bit_alu_5_x, n1_bit_alu_6_carry_out,
       n1_bit_alu_6_gro, n1_bit_alu_6_lso, n1_bit_alu_6_neo, n1_bit_alu_6_not_zero_out, n1_bit_alu_6_out_31,
       n1_bit_alu_6_out_32, n1_bit_alu_6_out_33, n1_bit_alu_6_out_34, n1_bit_alu_6_out_35,
       n1_bit_alu_6_out_36, n1_bit_alu_6_out_37, n1_bit_alu_6_out_38, n1_bit_alu_6_out_39,
       n1_bit_alu_6_out_40, n1_bit_alu_6_out_41, n1_bit_alu_6_out_43, n1_bit_alu_6_out_44, n1_bit_alu_6_slao,
       n1_bit_alu_6_slbo, n1_bit_alu_6_srao, n1_bit_alu_6_srbo, n1_bit_alu_6_x, n1_bit_alu_7_carry_out,
       n1_bit_alu_7_gro, n1_bit_alu_7_lso, n1_bit_alu_7_neo, n1_bit_alu_7_not_zero_out, n1_bit_alu_7_out_31,
       n1_bit_alu_7_out_32, n1_bit_alu_7_out_33, n1_bit_alu_7_out_34, n1_bit_alu_7_out_35,
       n1_bit_alu_7_out_36, n1_bit_alu_7_out_37, n1_bit_alu_7_out_38, n1_bit_alu_7_out_39,
       n1_bit_alu_7_out_40, n1_bit_alu_7_out_41, n1_bit_alu_7_out_43, n1_bit_alu_7_out_44, n1_bit_alu_7_slao,
       n1_bit_alu_7_slbo, n1_bit_alu_7_srao, n1_bit_alu_7_srbo, n1_bit_alu_7_x, n1_bit_alu_8_carry_out,
       n1_bit_alu_8_gro, n1_bit_alu_8_lso, n1_bit_alu_8_neo, n1_bit_alu_8_not_zero_out, n1_bit_alu_8_out_39,
       n1_bit_alu_8_slao, n1_bit_alu_8_srao, n1_bit_alu_8_srbo, n1_bit_alu_8_x, n8_bit_multiplier_1_overflow,
       n8_bit_multiplier_1_x0, n8_bit_multiplier_1_x1, n8_bit_multiplier_1_x2, n8_bit_multiplier_1_x3,
       n8_bit_multiplier_1_x4, n8_bit_multiplier_1_x5, n8_bit_multiplier_1_x6, n8_bit_multiplier_1_x7;

  _8_bit_Multiplier u_8_bit_multiplier_1 (
    .A0(B0), .A1(B1), .A2(B2), .A3(B3), .A4(B4), .A5(B5), .A6(B6), .A7(B7), .X0(n8_bit_multiplier_1_x0),
    .X1(n8_bit_multiplier_1_x1), .X2(n8_bit_multiplier_1_x2), .X3(n8_bit_multiplier_1_x3),
    .X4(n8_bit_multiplier_1_x4), .X5(n8_bit_multiplier_1_x5), .X6(n8_bit_multiplier_1_x6),
    .X7(n8_bit_multiplier_1_x7), .Overflow(n8_bit_multiplier_1_overflow), .B7(A7), .B6(A6), .B5(A5), .B4(A4),
    .B3(A3), .B2(A2), .B1(A1), .B0(A0));
  and and_1 (and_1_out, n1_bit_alu_1_srao, Shift_Loop);
  and and_2 (and_2_out, n1_bit_alu_1_srbo, Shift_Loop);
  and and_3 (and_3_out, Shift_Loop, n1_bit_alu_8_out_39);
  and and_4 (and_4_out, Shift_Loop, n1_bit_alu_8_slao);
  _1_bit_ALU u_1_bit_alu_1 (
    .A_2(A0), .B_2(B0), .X(n1_bit_alu_1_x), .A_invert(A_Invert), .B_invert(B_Invert), .And(AND), .Or(OR),
    .A(A), .B(B), .SRAO(n1_bit_alu_1_srao), .SRBO(n1_bit_alu_1_srbo), .SRA(Shift_A_Right),
    .SRB(Shift_B_Right), .SLAI(and_4_out), .SLBI(and_3_out), .SLA(Shift_A_Left), .SLB(Shift_B_Left),
    .XOr(XOR), .NEO(Not_Equal), .GRO(B_Greater_A), .LSO(A_Greater_B), .Carry_in(Increment), .Add(ADD),
    .X_invert(X_Invert), .out_31(n1_bit_alu_1_out_31), .out_32(n1_bit_alu_1_out_32),
    .out_33(n1_bit_alu_1_out_33), .out_34(n1_bit_alu_1_out_34), .out_35(n1_bit_alu_1_out_35),
    .out_36(n1_bit_alu_1_out_36), .SRAI(n1_bit_alu_2_srao), .SRBI(n1_bit_alu_2_srbo),
    .out_37(n1_bit_alu_1_out_37), .out_38(n1_bit_alu_1_out_38), .SLAO(n1_bit_alu_1_slao),
    .SLBO(n1_bit_alu_1_slbo), .out_39(n1_bit_alu_1_out_39), .out_40(n1_bit_alu_1_out_40),
    .out_41(n1_bit_alu_1_out_41), .NEI(n1_bit_alu_2_neo), .GRI(n1_bit_alu_2_gro), .LSI(n1_bit_alu_2_lso),
    .Carry_out(n1_bit_alu_1_carry_out), .out_43(n1_bit_alu_1_out_43), .out_44(n1_bit_alu_1_out_44),
    .Not_Zero_In(1'b0), .Not_Zero_Out(n1_bit_alu_1_not_zero_out));
  _1_bit_ALU u_1_bit_alu_2 (
    .A_2(A1), .B_2(B1), .X(n1_bit_alu_2_x), .A_invert(n1_bit_alu_1_out_31), .B_invert(n1_bit_alu_1_out_32),
    .And(n1_bit_alu_1_out_33), .Or(n1_bit_alu_1_out_34), .A(n1_bit_alu_1_out_35), .B(n1_bit_alu_1_out_36),
    .SRAO(n1_bit_alu_2_srao), .SRBO(n1_bit_alu_2_srbo), .SRA(n1_bit_alu_1_out_37), .SRB(n1_bit_alu_1_out_38),
    .SLAI(n1_bit_alu_1_slao), .SLBI(n1_bit_alu_1_slbo), .SLA(n1_bit_alu_1_out_39), .SLB(n1_bit_alu_1_out_40),
    .XOr(n1_bit_alu_1_out_41), .NEO(n1_bit_alu_2_neo), .GRO(n1_bit_alu_2_gro), .LSO(n1_bit_alu_2_lso),
    .Carry_in(n1_bit_alu_1_carry_out), .Add(n1_bit_alu_1_out_43), .X_invert(n1_bit_alu_1_out_44),
    .out_31(n1_bit_alu_2_out_31), .out_32(n1_bit_alu_2_out_32), .out_33(n1_bit_alu_2_out_33),
    .out_34(n1_bit_alu_2_out_34), .out_35(n1_bit_alu_2_out_35), .out_36(n1_bit_alu_2_out_36),
    .SRAI(n1_bit_alu_3_srao), .SRBI(n1_bit_alu_3_srbo), .out_37(n1_bit_alu_2_out_37),
    .out_38(n1_bit_alu_2_out_38), .SLAO(n1_bit_alu_2_slao), .SLBO(n1_bit_alu_2_slbo),
    .out_39(n1_bit_alu_2_out_39), .out_40(n1_bit_alu_2_out_40), .out_41(n1_bit_alu_2_out_41),
    .NEI(n1_bit_alu_3_neo), .GRI(n1_bit_alu_3_gro), .LSI(n1_bit_alu_3_lso),
    .Carry_out(n1_bit_alu_2_carry_out), .out_43(n1_bit_alu_2_out_43), .out_44(n1_bit_alu_2_out_44),
    .Not_Zero_In(n1_bit_alu_1_not_zero_out), .Not_Zero_Out(n1_bit_alu_2_not_zero_out));
  _1_bit_ALU u_1_bit_alu_3 (
    .A_2(A2), .B_2(B2), .X(n1_bit_alu_3_x), .A_invert(n1_bit_alu_2_out_31), .B_invert(n1_bit_alu_2_out_32),
    .And(n1_bit_alu_2_out_33), .Or(n1_bit_alu_2_out_34), .A(n1_bit_alu_2_out_35), .B(n1_bit_alu_2_out_36),
    .SRAO(n1_bit_alu_3_srao), .SRBO(n1_bit_alu_3_srbo), .SRA(n1_bit_alu_2_out_37), .SRB(n1_bit_alu_2_out_38),
    .SLAI(n1_bit_alu_2_slao), .SLBI(n1_bit_alu_2_slbo), .SLA(n1_bit_alu_2_out_39), .SLB(n1_bit_alu_2_out_40),
    .XOr(n1_bit_alu_2_out_41), .NEO(n1_bit_alu_3_neo), .GRO(n1_bit_alu_3_gro), .LSO(n1_bit_alu_3_lso),
    .Carry_in(n1_bit_alu_2_carry_out), .Add(n1_bit_alu_2_out_43), .X_invert(n1_bit_alu_2_out_44),
    .out_31(n1_bit_alu_3_out_31), .out_32(n1_bit_alu_3_out_32), .out_33(n1_bit_alu_3_out_33),
    .out_34(n1_bit_alu_3_out_34), .out_35(n1_bit_alu_3_out_35), .out_36(n1_bit_alu_3_out_36),
    .SRAI(n1_bit_alu_4_srao), .SRBI(n1_bit_alu_4_srbo), .out_37(n1_bit_alu_3_out_37),
    .out_38(n1_bit_alu_3_out_38), .SLAO(n1_bit_alu_3_slao), .SLBO(n1_bit_alu_3_slbo),
    .out_39(n1_bit_alu_3_out_39), .out_40(n1_bit_alu_3_out_40), .out_41(n1_bit_alu_3_out_41),
    .NEI(n1_bit_alu_4_neo), .GRI(n1_bit_alu_4_gro), .LSI(n1_bit_alu_4_lso),
    .Carry_out(n1_bit_alu_3_carry_out), .out_43(n1_bit_alu_3_out_43), .out_44(n1_bit_alu_3_out_44),
    .Not_Zero_In(n1_bit_alu_2_not_zero_out), .Not_Zero_Out(n1_bit_alu_3_not_zero_out));
  _1_bit_ALU u_1_bit_alu_4 (
    .A_2(A3), .B_2(B3), .X(n1_bit_alu_4_x), .A_invert(n1_bit_alu_3_out_31), .B_invert(n1_bit_alu_3_out_32),
    .And(n1_bit_alu_3_out_33), .Or(n1_bit_alu_3_out_34), .A(n1_bit_alu_3_out_35), .B(n1_bit_alu_3_out_36),
    .SRAO(n1_bit_alu_4_srao), .SRBO(n1_bit_alu_4_srbo), .SRA(n1_bit_alu_3_out_37), .SRB(n1_bit_alu_3_out_38),
    .SLAI(n1_bit_alu_3_slao), .SLBI(n1_bit_alu_3_slbo), .SLA(n1_bit_alu_3_out_39), .SLB(n1_bit_alu_3_out_40),
    .XOr(n1_bit_alu_3_out_41), .NEO(n1_bit_alu_4_neo), .GRO(n1_bit_alu_4_gro), .LSO(n1_bit_alu_4_lso),
    .Carry_in(n1_bit_alu_3_carry_out), .Add(n1_bit_alu_3_out_43), .X_invert(n1_bit_alu_3_out_44),
    .out_31(n1_bit_alu_4_out_31), .out_32(n1_bit_alu_4_out_32), .out_33(n1_bit_alu_4_out_33),
    .out_34(n1_bit_alu_4_out_34), .out_35(n1_bit_alu_4_out_35), .out_36(n1_bit_alu_4_out_36),
    .SRAI(n1_bit_alu_5_srao), .SRBI(n1_bit_alu_5_srbo), .out_37(n1_bit_alu_4_out_37),
    .out_38(n1_bit_alu_4_out_38), .SLAO(n1_bit_alu_4_slao), .SLBO(n1_bit_alu_4_slbo),
    .out_39(n1_bit_alu_4_out_39), .out_40(n1_bit_alu_4_out_40), .out_41(n1_bit_alu_4_out_41),
    .NEI(n1_bit_alu_5_neo), .GRI(n1_bit_alu_5_gro), .LSI(n1_bit_alu_5_lso),
    .Carry_out(n1_bit_alu_4_carry_out), .out_43(n1_bit_alu_4_out_43), .out_44(n1_bit_alu_4_out_44),
    .Not_Zero_In(n1_bit_alu_3_not_zero_out), .Not_Zero_Out(n1_bit_alu_4_not_zero_out));
  _1_bit_ALU u_1_bit_alu_5 (
    .A_2(A4), .B_2(B4), .X(n1_bit_alu_5_x), .A_invert(n1_bit_alu_4_out_31), .B_invert(n1_bit_alu_4_out_32),
    .And(n1_bit_alu_4_out_33), .Or(n1_bit_alu_4_out_34), .A(n1_bit_alu_4_out_35), .B(n1_bit_alu_4_out_36),
    .SRAO(n1_bit_alu_5_srao), .SRBO(n1_bit_alu_5_srbo), .SRA(n1_bit_alu_4_out_37), .SRB(n1_bit_alu_4_out_38),
    .SLAI(n1_bit_alu_4_slao), .SLBI(n1_bit_alu_4_slbo), .SLA(n1_bit_alu_4_out_39), .SLB(n1_bit_alu_4_out_40),
    .XOr(n1_bit_alu_4_out_41), .NEO(n1_bit_alu_5_neo), .GRO(n1_bit_alu_5_gro), .LSO(n1_bit_alu_5_lso),
    .Carry_in(n1_bit_alu_4_carry_out), .Add(n1_bit_alu_4_out_43), .X_invert(n1_bit_alu_4_out_44),
    .out_31(n1_bit_alu_5_out_31), .out_32(n1_bit_alu_5_out_32), .out_33(n1_bit_alu_5_out_33),
    .out_34(n1_bit_alu_5_out_34), .out_35(n1_bit_alu_5_out_35), .out_36(n1_bit_alu_5_out_36),
    .SRAI(n1_bit_alu_6_srao), .SRBI(n1_bit_alu_6_srbo), .out_37(n1_bit_alu_5_out_37),
    .out_38(n1_bit_alu_5_out_38), .SLAO(n1_bit_alu_5_slao), .SLBO(n1_bit_alu_5_slbo),
    .out_39(n1_bit_alu_5_out_39), .out_40(n1_bit_alu_5_out_40), .out_41(n1_bit_alu_5_out_41),
    .NEI(n1_bit_alu_6_neo), .GRI(n1_bit_alu_6_gro), .LSI(n1_bit_alu_6_lso),
    .Carry_out(n1_bit_alu_5_carry_out), .out_43(n1_bit_alu_5_out_43), .out_44(n1_bit_alu_5_out_44),
    .Not_Zero_In(n1_bit_alu_4_not_zero_out), .Not_Zero_Out(n1_bit_alu_5_not_zero_out));
  _1_bit_ALU u_1_bit_alu_6 (
    .A_2(A5), .B_2(B5), .X(n1_bit_alu_6_x), .A_invert(n1_bit_alu_5_out_31), .B_invert(n1_bit_alu_5_out_32),
    .And(n1_bit_alu_5_out_33), .Or(n1_bit_alu_5_out_34), .A(n1_bit_alu_5_out_35), .B(n1_bit_alu_5_out_36),
    .SRAO(n1_bit_alu_6_srao), .SRBO(n1_bit_alu_6_srbo), .SRA(n1_bit_alu_5_out_37), .SRB(n1_bit_alu_5_out_38),
    .SLAI(n1_bit_alu_5_slao), .SLBI(n1_bit_alu_5_slbo), .SLA(n1_bit_alu_5_out_39), .SLB(n1_bit_alu_5_out_40),
    .XOr(n1_bit_alu_5_out_41), .NEO(n1_bit_alu_6_neo), .GRO(n1_bit_alu_6_gro), .LSO(n1_bit_alu_6_lso),
    .Carry_in(n1_bit_alu_5_carry_out), .Add(n1_bit_alu_5_out_43), .X_invert(n1_bit_alu_5_out_44),
    .out_31(n1_bit_alu_6_out_31), .out_32(n1_bit_alu_6_out_32), .out_33(n1_bit_alu_6_out_33),
    .out_34(n1_bit_alu_6_out_34), .out_35(n1_bit_alu_6_out_35), .out_36(n1_bit_alu_6_out_36),
    .SRAI(n1_bit_alu_7_srao), .SRBI(n1_bit_alu_7_srbo), .out_37(n1_bit_alu_6_out_37),
    .out_38(n1_bit_alu_6_out_38), .SLAO(n1_bit_alu_6_slao), .SLBO(n1_bit_alu_6_slbo),
    .out_39(n1_bit_alu_6_out_39), .out_40(n1_bit_alu_6_out_40), .out_41(n1_bit_alu_6_out_41),
    .NEI(n1_bit_alu_7_neo), .GRI(n1_bit_alu_7_gro), .LSI(n1_bit_alu_7_lso),
    .Carry_out(n1_bit_alu_6_carry_out), .out_43(n1_bit_alu_6_out_43), .out_44(n1_bit_alu_6_out_44),
    .Not_Zero_In(n1_bit_alu_5_not_zero_out), .Not_Zero_Out(n1_bit_alu_6_not_zero_out));
  _1_bit_ALU u_1_bit_alu_7 (
    .A_2(A6), .B_2(B6), .X(n1_bit_alu_7_x), .A_invert(n1_bit_alu_6_out_31), .B_invert(n1_bit_alu_6_out_32),
    .And(n1_bit_alu_6_out_33), .Or(n1_bit_alu_6_out_34), .A(n1_bit_alu_6_out_35), .B(n1_bit_alu_6_out_36),
    .SRAO(n1_bit_alu_7_srao), .SRBO(n1_bit_alu_7_srbo), .SRA(n1_bit_alu_6_out_37), .SRB(n1_bit_alu_6_out_38),
    .SLAI(n1_bit_alu_6_slao), .SLBI(n1_bit_alu_6_slbo), .SLA(n1_bit_alu_6_out_39), .SLB(n1_bit_alu_6_out_40),
    .XOr(n1_bit_alu_6_out_41), .NEO(n1_bit_alu_7_neo), .GRO(n1_bit_alu_7_gro), .LSO(n1_bit_alu_7_lso),
    .Carry_in(n1_bit_alu_6_carry_out), .Add(n1_bit_alu_6_out_43), .X_invert(n1_bit_alu_6_out_44),
    .out_31(n1_bit_alu_7_out_31), .out_32(n1_bit_alu_7_out_32), .out_33(n1_bit_alu_7_out_33),
    .out_34(n1_bit_alu_7_out_34), .out_35(n1_bit_alu_7_out_35), .out_36(n1_bit_alu_7_out_36),
    .SRAI(n1_bit_alu_8_srao), .SRBI(n1_bit_alu_8_srbo), .out_37(n1_bit_alu_7_out_37),
    .out_38(n1_bit_alu_7_out_38), .SLAO(n1_bit_alu_7_slao), .SLBO(n1_bit_alu_7_slbo),
    .out_39(n1_bit_alu_7_out_39), .out_40(n1_bit_alu_7_out_40), .out_41(n1_bit_alu_7_out_41),
    .NEI(n1_bit_alu_8_neo), .GRI(n1_bit_alu_8_gro), .LSI(n1_bit_alu_8_lso),
    .Carry_out(n1_bit_alu_7_carry_out), .out_43(n1_bit_alu_7_out_43), .out_44(n1_bit_alu_7_out_44),
    .Not_Zero_In(n1_bit_alu_6_not_zero_out), .Not_Zero_Out(n1_bit_alu_7_not_zero_out));
  _1_bit_ALU u_1_bit_alu_8 (
    .A_2(A7), .B_2(B7), .X(n1_bit_alu_8_x), .A_invert(n1_bit_alu_7_out_31), .B_invert(n1_bit_alu_7_out_32),
    .And(n1_bit_alu_7_out_33), .Or(n1_bit_alu_7_out_34), .A(n1_bit_alu_7_out_35), .B(n1_bit_alu_7_out_36),
    .SRAO(n1_bit_alu_8_srao), .SRBO(n1_bit_alu_8_srbo), .SRA(n1_bit_alu_7_out_37), .SRB(n1_bit_alu_7_out_38),
    .SLAI(n1_bit_alu_7_slao), .SLBI(n1_bit_alu_7_slbo), .SLA(n1_bit_alu_7_out_39), .SLB(n1_bit_alu_7_out_40),
    .XOr(n1_bit_alu_7_out_41), .NEO(n1_bit_alu_8_neo), .GRO(n1_bit_alu_8_gro), .LSO(n1_bit_alu_8_lso),
    .Carry_in(n1_bit_alu_7_carry_out), .Add(n1_bit_alu_7_out_43), .X_invert(n1_bit_alu_7_out_44),
    .SRAI(and_1_out), .out_37(and_2_out), .SLAO(n1_bit_alu_8_slao), .out_39(n1_bit_alu_8_out_39), .NEI(1'b0),
    .GRI(1'b0), .LSI(1'b0), .Carry_out(n1_bit_alu_8_carry_out), .Not_Zero_In(n1_bit_alu_7_not_zero_out),
    .Not_Zero_Out(n1_bit_alu_8_not_zero_out));  // open: out_31, out_32, out_33, out_34, out_35, out_36, SRBI, out_38, SLBO, out_40, out_41, out_43, out_44
  not not_1 (Zero, n1_bit_alu_8_not_zero_out);
  or or_1 (Overflow, n1_bit_alu_8_carry_out, n8_bit_multiplier_1_overflow);
  _2_Way_Multiplexor u_2_way_multiplexor_1 (
    ._0(n1_bit_alu_1_x), ._1(n1_bit_alu_2_x), ._2(n1_bit_alu_3_x), ._3(n1_bit_alu_4_x), ._4(n1_bit_alu_5_x),
    ._5(n1_bit_alu_6_x), ._6(n1_bit_alu_7_x), ._7(n1_bit_alu_8_x), ._0_2(n8_bit_multiplier_1_x0),
    ._1_2(n8_bit_multiplier_1_x1), ._2_2(n8_bit_multiplier_1_x2), ._3_2(n8_bit_multiplier_1_x3),
    ._4_2(n8_bit_multiplier_1_x4), ._5_2(n8_bit_multiplier_1_x5), ._6_2(n8_bit_multiplier_1_x6),
    ._7_2(n8_bit_multiplier_1_x7), .S(Multiply), ._0_3(X0), ._1_3(X1), ._2_3(X2), ._3_3(X3), ._4_3(X4),
    ._5_3(X5), ._6_3(X6), ._7_3(X7));
endmodule

module D_Latch (
  input  Clock,
  input  Data,
  output Out
);

  wire and_1_out, and_2_out, not_1_out, not_2_out, not_3_out, or_1_out, or_2_out, undriven, undriven_2;

  D_Flip_Flop #(.trigger("high")) d_ff_1 (.clk(Clock), .D(Data), .Q(Out));  // open: Qn, preset, en, reset
  not not_1 (not_1_out, undriven_2);
  and and_1 (and_1_out, undriven, undriven_2);
  or or_1 (or_1_out, and_1_out, not_3_out);
  not not_2 (not_2_out, or_1_out);
  or or_2 (or_2_out, not_2_out, and_2_out);
  not not_3 (not_3_out, or_2_out);
  and and_2 (and_2_out, not_1_out, undriven);
endmodule

module _4_bit_Decoder (
  input  _0,
  input  _1,
  input  _2,
  input  _3,
  output _0_2,
  output _1_2,
  output _2_2,
  output _3_2,
  output _4,
  output _5,
  output _6,
  output _7,
  output _8,
  output _9,
  output _10,
  output _11,
  output _12,
  output _13,
  output _14,
  output _15
);

  wire and_1_out, and_3_out, and_4_out, and_6_out, and_7_out, and_9_out, and_10_out, and_12_out, and_13_out,
       and_15_out, and_16_out, and_18_out, and_19_out, and_21_out, and_22_out, and_24_out, and_25_out,
       and_27_out, and_28_out, and_30_out, and_31_out, and_33_out, and_34_out, and_36_out, and_37_out,
       and_39_out, and_40_out, and_42_out, and_43_out, and_45_out, and_46_out, and_48_out, not_1_out,
       not_2_out, not_3_out, not_4_out, not_5_out, not_6_out, not_7_out, not_8_out, not_9_out, not_10_out,
       not_11_out, not_12_out, not_13_out, not_14_out, not_15_out, not_16_out, not_17_out, not_18_out,
       not_19_out, not_20_out, not_21_out, not_22_out, not_23_out, not_24_out, not_25_out, not_26_out,
       not_27_out, not_28_out, not_29_out, not_30_out, not_31_out, not_32_out;

  and and_1 (and_1_out, not_1_out, not_2_out);
  not not_1 (not_1_out, _3);
  not not_2 (not_2_out, _2);
  and and_2 (_0_2, and_1_out, and_4_out);
  and and_3 (and_3_out, not_5_out, not_4_out);
  and and_4 (and_4_out, not_6_out, not_3_out);
  not not_3 (not_3_out, _0);
  not not_4 (not_4_out, _2);
  not not_5 (not_5_out, _3);
  not not_6 (not_6_out, _1);
  and and_5 (_1_2, and_3_out, and_6_out);
  and and_6 (and_6_out, not_7_out, _0);
  and and_7 (and_7_out, not_8_out, not_9_out);
  not not_7 (not_7_out, _1);
  not not_8 (not_8_out, _3);
  not not_9 (not_9_out, _2);
  and and_8 (_2_2, and_7_out, and_10_out);
  and and_9 (and_9_out, not_12_out, not_11_out);
  and and_10 (and_10_out, _1, not_10_out);
  not not_10 (not_10_out, _0);
  not not_11 (not_11_out, _2);
  not not_12 (not_12_out, _3);
  and and_11 (_3_2, and_9_out, and_12_out);
  and and_12 (and_12_out, _1, _0);
  and and_13 (and_13_out, not_13_out, _2);
  not not_13 (not_13_out, _3);
  and and_14 (_4, and_13_out, and_15_out);
  and and_15 (and_15_out, not_15_out, not_16_out);
  and and_16 (and_16_out, not_14_out, _2);
  not not_14 (not_14_out, _3);
  not not_15 (not_15_out, _1);
  not not_16 (not_16_out, _0);
  and and_17 (_5, and_16_out, and_19_out);
  and and_18 (and_18_out, not_18_out, _2);
  and and_19 (and_19_out, not_17_out, _0);
  not not_17 (not_17_out, _1);
  not not_18 (not_18_out, _3);
  and and_20 (_6, and_18_out, and_21_out);
  and and_21 (and_21_out, _1, not_20_out);
  and and_22 (and_22_out, not_19_out, _2);
  not not_19 (not_19_out, _3);
  not not_20 (not_20_out, _0);
  and and_23 (_7, and_22_out, and_25_out);
  and and_24 (and_24_out, _3, not_21_out);
  and and_25 (and_25_out, _1, _0);
  not not_21 (not_21_out, _2);
  and and_26 (_8, and_24_out, and_27_out);
  and and_27 (and_27_out, not_22_out, not_24_out);
  and and_28 (and_28_out, _3, not_23_out);
  not not_22 (not_22_out, _1);
  not not_23 (not_23_out, _2);
  not not_24 (not_24_out, _0);
  and and_29 (_9, and_28_out, and_30_out);
  and and_30 (and_30_out, not_25_out, _0);
  and and_31 (and_31_out, _3, not_26_out);
  not not_25 (not_25_out, _1);
  not not_26 (not_26_out, _2);
  and and_32 (_10, and_31_out, and_34_out);
  and and_33 (and_33_out, _3, not_28_out);
  and and_34 (and_34_out, _1, not_27_out);
  not not_27 (not_27_out, _0);
  not not_28 (not_28_out, _2);
  and and_35 (_11, and_33_out, and_37_out);
  and and_36 (and_36_out, _3, _2);
  and and_37 (and_37_out, _1, _0);
  and and_38 (_12, and_36_out, and_40_out);
  and and_39 (and_39_out, _3, _2);
  and and_40 (and_40_out, not_29_out, not_30_out);
  not not_29 (not_29_out, _1);
  not not_30 (not_30_out, _0);
  and and_41 (_13, and_39_out, and_42_out);
  and and_42 (and_42_out, not_31_out, _0);
  and and_43 (and_43_out, _3, _2);
  not not_31 (not_31_out, _1);
  and and_44 (_14, and_43_out, and_45_out);
  and and_45 (and_45_out, _1, not_32_out);
  and and_46 (and_46_out, _3, _2);
  not not_32 (not_32_out, _0);
  and and_47 (_15, and_46_out, and_48_out);
  and and_48 (and_48_out, _1, _0);
endmodule

module _8_bit_Register (
  input  _0,
  input  _1,
  input  _2,
  input  _3,
  input  _4,
  input  _5,
  input  _6,
  input  _7,
  input  Reset,
  input  Clock,
  output [7:0] _0_2,
  output _0_3,
  output _1_2,
  output _2_2,
  output _3_2,
  output _4_2,
  output _5_2,
  output _6_2,
  output _7_2
);

  wire and_1_out, and_2_out, and_3_out, and_4_out, and_5_out, and_6_out, and_7_out, and_8_out, and_9_out,
       not_1_out, or_1_out;

  and and_1 (and_1_out, not_1_out, or_1_out);
  not not_1 (not_1_out, Reset);
  and and_2 (and_2_out, _0, and_1_out);
  and and_3 (and_3_out, _1, and_1_out);
  and and_4 (and_4_out, _2, and_1_out);
  and and_5 (and_5_out, _3, and_1_out);
  and and_6 (and_6_out, _4, and_1_out);
  and and_7 (and_7_out, _5, and_1_out);
  and and_8 (and_8_out, _6, and_1_out);
  and and_9 (and_9_out, _7, and_1_out);
  or or_1 (or_1_out, Reset, Clock);
  D_Latch d_latch_1 (.Clock(or_1_out), .Data(and_2_out), .Out(_0_2[0]));
  D_Latch d_latch_2 (.Clock(or_1_out), .Data(and_3_out), .Out(_0_2[1]));
  D_Latch d_latch_3 (.Clock(or_1_out), .Data(and_4_out), .Out(_0_2[2]));
  D_Latch d_latch_4 (.Clock(or_1_out), .Data(and_5_out), .Out(_0_2[3]));
  D_Latch d_latch_5 (.Clock(or_1_out), .Data(and_6_out), .Out(_0_2[4]));
  D_Latch d_latch_6 (.Clock(or_1_out), .Data(and_7_out), .Out(_0_2[5]));
  D_Latch d_latch_7 (.Clock(or_1_out), .Data(and_8_out), .Out(_0_2[6]));
  D_Latch d_latch_8 (.Clock(or_1_out), .Data(and_9_out), .Out(_0_2[7]));

  assign _0_3 = _0_2[0];
  assign _1_2 = _0_2[1];
  assign _2_2 = _0_2[2];
  assign _3_2 = _0_2[3];
  assign _4_2 = _0_2[4];
  assign _5_2 = _0_2[5];
  assign _6_2 = _0_2[6];
  assign _7_2 = _0_2[7];
endmodule

module Register (
  input  Data,
  input  Clock,
  output Clock_Out,
  output X
);

  wire d_latch_1_out;

  D_Latch d_latch_1 (.Clock(Clock), .Data(Data), .Out(d_latch_1_out));
  and and_1 (X, Clock, d_latch_1_out);

  assign Clock_Out = Clock;
endmodule

module _8_bit_Adder (
  input  Increment,
  input  A0,
  input  B0,
  input  A1,
  input  B1,
  input  A2,
  input  B2,
  input  A3,
  input  B3,
  input  A4,
  input  B4,
  input  A5,
  input  B5,
  input  A6,
  input  B6,
  input  A7,
  input  B7,
  output X0,
  output X1,
  output X2,
  output X3,
  output X4,
  output X5,
  output X6,
  output X7,
  output Carry_Out
);

  wire full_adder_1_carry_out, full_adder_2_carry_out, full_adder_3_carry_out, full_adder_4_carry_out,
       full_adder_5_carry_out, full_adder_6_carry_out, full_adder_7_carry_out;

  Full_Adder full_adder_1 (.A(A0), .B(B0), .X(X0), .Carry_In(Increment), .Carry_Out(full_adder_1_carry_out));
  Full_Adder full_adder_2 (
    .A(A1), .B(B1), .X(X1), .Carry_In(full_adder_1_carry_out), .Carry_Out(full_adder_2_carry_out));
  Full_Adder full_adder_3 (
    .A(A2), .B(B2), .X(X2), .Carry_In(full_adder_2_carry_out), .Carry_Out(full_adder_3_carry_out));
  Full_Adder full_adder_4 (
    .A(A3), .B(B3), .X(X3), .Carry_In(full_adder_3_carry_out), .Carry_Out(full_adder_4_carry_out));
  Full_Adder full_adder_5 (
    .A(A4), .B(B4), .X(X4), .Carry_In(full_adder_4_carry_out), .Carry_Out(full_adder_5_carry_out));
  Full_Adder full_adder_6 (
    .A(A5), .B(B5), .X(X5), .Carry_In(full_adder_5_carry_out), .Carry_Out(full_adder_6_carry_out));
  Full_Adder full_adder_7 (
    .A(A6), .B(B6), .X(X6), .Carry_In(full_adder_6_carry_out), .Carry_Out(full_adder_7_carry_out));
  Full_Adder full_adder_8 (.A(A7), .B(B7), .X(X7), .Carry_In(full_adder_7_carry_out), .Carry_Out(Carry_Out));
endmodule

module Full_Adder (
  input  Carry_In,
  input  A,
  input  B,
  output X,
  output Carry_Out
);

  wire and_1_out, and_2_out, and_3_out, not_1_out, not_2_out, or_1_out, or_3_out;

  or or_1 (or_1_out, A, B);
  and and_1 (and_1_out, B, A);
  and and_2 (and_2_out, or_1_out, not_1_out);
  not not_1 (not_1_out, and_1_out);
  or or_2 (Carry_Out, and_1_out, and_3_out);
  or or_3 (or_3_out, Carry_In, and_2_out);
  not not_2 (not_2_out, and_3_out);
  and and_3 (and_3_out, and_2_out, Carry_In);
  and and_4 (X, or_3_out, not_2_out);
endmodule

module _8_bit_Counter__Adding (
  input  Reset,
  input  Count,
  input  Set,
  input  _7,
  input  _5,
  input  _3,
  input  _1,
  input  _6,
  input  _4,
  input  _2,
  input  _0,
  output _0_2,
  output _1_2,
  output _2_2,
  output _3_2,
  output _4_2,
  output _5_2,
  output _6_2,
  output _7_2,
  output Carry_Out
);

  wire n2_way_multiplexor_1__0_3, n2_way_multiplexor_1__1_3, n2_way_multiplexor_1__2_3,
       n2_way_multiplexor_1__3_3, n2_way_multiplexor_1__4_3, n2_way_multiplexor_1__5_3,
       n2_way_multiplexor_1__6_3, n2_way_multiplexor_1__7_3, n8_bit_adder_1_x0, n8_bit_adder_1_x1,
       n8_bit_adder_1_x2, n8_bit_adder_1_x3, n8_bit_adder_1_x4, n8_bit_adder_1_x5, n8_bit_adder_1_x6,
       n8_bit_adder_1_x7, n8_bit_register_1_p10, n8_bit_register_1_p11, n8_bit_register_1_p12,
       n8_bit_register_1_p13, n8_bit_register_1_p14, n8_bit_register_1_p15, n8_bit_register_1_p16,
       n8_bit_register_1_p17, n8_bit_register_1_p18, n8_bit_register_2_p10;

  // _8_bit_Register 8_bit_register_1: pin names not known; wires that end beside it: _0_2, _1_2, _2_2, _3_2, _4_2, _5_2, _6_2, _7_2, Reset, n8_bit_register_1_p10, n8_bit_register_1_p11, n8_bit_register_1_p12, n8_bit_register_1_p13, n8_bit_register_1_p14, n8_bit_register_1_p15, n8_bit_register_1_p16, n8_bit_register_1_p17, n8_bit_register_1_p18
  _8_bit_Adder u_8_bit_adder_1 (
    .A0(n8_bit_register_1_p11), .B0(1'b0), .A1(n8_bit_register_1_p12), .B1(1'b0), .A2(n8_bit_register_1_p13),
    .B2(1'b0), .A3(n8_bit_register_1_p14), .B3(1'b0), .A4(n8_bit_register_1_p15), .B4(1'b0),
    .A5(n8_bit_register_1_p16), .B5(1'b0), .A6(n8_bit_register_1_p17), .B6(1'b0), .A7(n8_bit_register_1_p18),
    .B7(1'b0), .X0(n8_bit_adder_1_x0), .X1(n8_bit_adder_1_x1), .X2(n8_bit_adder_1_x2),
    .X3(n8_bit_adder_1_x3), .X4(n8_bit_adder_1_x4), .X5(n8_bit_adder_1_x5), .X6(n8_bit_adder_1_x6),
    .X7(n8_bit_adder_1_x7), .Increment(1'b1), .Carry_Out(Carry_Out));
  _2_Way_Multiplexor u_2_way_multiplexor_1 (
    ._0(n8_bit_adder_1_x0), ._1(n8_bit_adder_1_x1), ._2(n8_bit_adder_1_x2), ._3(n8_bit_adder_1_x3),
    ._4(n8_bit_adder_1_x4), ._5(n8_bit_adder_1_x5), ._6(n8_bit_adder_1_x6), ._7(n8_bit_adder_1_x7),
    ._0_2(_0), ._1_2(_1), ._2_2(_2), ._3_2(_3), ._4_2(_4), ._5_2(_5), ._6_2(_6), ._7_2(_7), .S(Set),
    ._0_3(n2_way_multiplexor_1__0_3), ._1_3(n2_way_multiplexor_1__1_3), ._2_3(n2_way_multiplexor_1__2_3),
    ._3_3(n2_way_multiplexor_1__3_3), ._4_3(n2_way_multiplexor_1__4_3), ._5_3(n2_way_multiplexor_1__5_3),
    ._6_3(n2_way_multiplexor_1__6_3), ._7_3(n2_way_multiplexor_1__7_3));
  // _8_bit_Register 8_bit_register_2: pin names not known; wires that end beside it: n2_way_multiplexor_1__0_3, n2_way_multiplexor_1__1_3, n2_way_multiplexor_1__2_3, n2_way_multiplexor_1__3_3, n2_way_multiplexor_1__4_3, n2_way_multiplexor_1__5_3, n2_way_multiplexor_1__6_3, n2_way_multiplexor_1__7_3, Reset, n8_bit_register_2_p10, _0_2, _1_2, _2_2, _3_2, _4_2, _5_2, _6_2, _7_2
  not not_1 (n8_bit_register_2_p10, n8_bit_register_1_p10);
  or or_1 (n8_bit_register_1_p10, Count, Set);
endmodule

module _2_Way_Multiplexor (
  input  _0,
  input  _1,
  input  _2,
  input  _3,
  input  _4,
  input  _5,
  input  _6,
  input  _7,
  input  S,
  input  _7_2,
  input  _6_2,
  input  _5_2,
  input  _4_2,
  input  _3_2,
  input  _2_2,
  input  _1_2,
  input  _0_2,
  output _0_3,
  output _1_3,
  output _2_3,
  output _3_3,
  output _4_3,
  output _5_3,
  output _6_3,
  output _7_3
);

  wire and_1_out, and_2_out, and_3_out, and_4_out, and_5_out, and_6_out, and_7_out, and_8_out, and_9_out,
       and_10_out, and_11_out, and_12_out, and_13_out, and_14_out, and_15_out, and_16_out, not_1_out;

  and and_1 (and_1_out, _0, not_1_out);
  and and_2 (and_2_out, _1, not_1_out);
  and and_3 (and_3_out, _2, not_1_out);
  and and_4 (and_4_out, _3, not_1_out);
  and and_5 (and_5_out, _4, not_1_out);
  and and_6 (and_6_out, _5, not_1_out);
  and and_7 (and_7_out, _6, not_1_out);
  and and_8 (and_8_out, _7, not_1_out);
  not not_1 (not_1_out, S);
  or or_1 (_7_3, and_8_out, and_9_out);
  and and_9 (and_9_out, _7_2, S);
  and and_10 (and_10_out, _6_2, S);
  or or_2 (_5_3, and_6_out, and_11_out);
  or or_3 (_6_3, and_7_out, and_10_out);
  and and_11 (and_11_out, _5_2, S);
  and and_12 (and_12_out, _4_2, S);
  or or_4 (_3_3, and_4_out, and_14_out);
  or or_5 (_4_3, and_5_out, and_12_out);
  and and_13 (and_13_out, _2_2, S);
  and and_14 (and_14_out, _3_2, S);
  or or_6 (_1_3, and_2_out, and_16_out);
  or or_7 (_2_3, and_3_out, and_13_out);
  and and_15 (and_15_out, _0_2, S);
  and and_16 (and_16_out, _1_2, S);
  or or_8 (_0_3, and_1_out, and_15_out);
endmodule

module _8_bit_Flip (
  input  _0,
  input  _0_2,
  input  _1,
  input  _1_2,
  input  _2,
  input  _2_2,
  input  _3,
  input  _3_2,
  input  _4,
  input  _4_2,
  input  _5,
  input  _5_2,
  input  _6,
  input  _6_2,
  input  _6_3,
  input  _6_4,
  output _0_3,
  output _0_4,
  output _1_3,
  output _1_4,
  output _2_3,
  output _2_4,
  output _3_3,
  output _3_4,
  output _4_3,
  output _4_4,
  output _5_3,
  output _5_4,
  output _6_5,
  output _6_6,
  output _6_7,
  output _6_8
);


  assign _0_3 = _0;
  assign _0_4 = _0_2;
  assign _1_3 = _1;
  assign _1_4 = _1_2;
  assign _2_3 = _2;
  assign _2_4 = _2_2;
  assign _3_3 = _3;
  assign _3_4 = _3_2;
  assign _4_3 = _4;
  assign _4_4 = _4_2;
  assign _5_3 = _5;
  assign _5_4 = _5_2;
  assign _6_5 = _6;
  assign _6_6 = _6_2;
  assign _6_7 = _6_3;
  assign _6_8 = _6_4;
endmodule

module _3_Way_Demultiplexer (
  input  _0,
  input  _1,
  input  _2,
  input  _3,
  input  _4,
  input  _5,
  input  _6,
  input  _7,
  input  S0,
  input  S1,
  output _7_2,
  output _6_2,
  output _5_2,
  output _4_2,
  output _3_2,
  output _2_2,
  output _1_2,
  output _0_2,
  output _0_3,
  output _1_3,
  output _2_3,
  output _3_3,
  output _4_3,
  output _5_3,
  output _6_3,
  output _7_3,
  output _7_4,
  output _6_4,
  output _5_4,
  output _4_4,
  output _3_4,
  output _2_4,
  output _1_4,
  output _0_4
);

  wire and_2_out, and_3_out, and_7_out, and_8_out, and_9_out, and_10_out, and_15_out, and_16_out, and_17_out,
       and_18_out, and_23_out, and_24_out, and_25_out, and_26_out, and_30_out, and_31_out, and_34_out,
       and_36_out, and_38_out, and_40_out, and_42_out, and_44_out, and_46_out, and_48_out, not_1_out,
       not_2_out, not_3_out;

  and and_1 (_7_2, not_3_out, and_2_out);
  and and_2 (and_2_out, _7, not_1_out);
  and and_3 (and_3_out, _7, S0);
  and and_4 (_7_4, S1, and_3_out);
  and and_5 (_6_2, not_3_out, and_8_out);
  and and_6 (_5_2, not_3_out, and_7_out);
  and and_7 (and_7_out, _5, not_1_out);
  and and_8 (and_8_out, _6, not_1_out);
  and and_9 (and_9_out, _6, S0);
  and and_10 (and_10_out, _5, S0);
  and and_11 (_6_4, S1, and_9_out);
  and and_12 (_5_4, S1, and_10_out);
  and and_13 (_3_2, not_3_out, and_16_out);
  and and_14 (_4_2, not_3_out, and_15_out);
  and and_15 (and_15_out, _4, not_1_out);
  and and_16 (and_16_out, _3, not_1_out);
  and and_17 (and_17_out, _4, S0);
  and and_18 (and_18_out, _3, S0);
  and and_19 (_4_4, S1, and_17_out);
  and and_20 (_3_4, S1, and_18_out);
  and and_21 (_2_2, not_3_out, and_23_out);
  and and_22 (_1_2, not_3_out, and_24_out);
  and and_23 (and_23_out, _2, not_1_out);
  and and_24 (and_24_out, _1, not_1_out);
  and and_25 (and_25_out, _2, S0);
  and and_26 (and_26_out, _1, S0);
  and and_27 (_2_4, S1, and_25_out);
  and and_28 (_1_4, S1, and_26_out);
  and and_29 (_0_2, not_3_out, and_30_out);
  and and_30 (and_30_out, _0, not_1_out);
  not not_1 (not_1_out, not_2_out);
  not not_2 (not_2_out, S0);
  and and_31 (and_31_out, _0, S0);
  and and_32 (_0_4, S1, and_31_out);
  not not_3 (not_3_out, S1);
  and and_33 (_0_3, S1, and_34_out);
  and and_34 (and_34_out, _0, not_2_out);
  and and_35 (_1_3, S1, and_36_out);
  and and_36 (and_36_out, _1, not_2_out);
  and and_37 (_2_3, S1, and_38_out);
  and and_38 (and_38_out, _2, not_2_out);
  and and_39 (_3_3, S1, and_40_out);
  and and_40 (and_40_out, _3, not_2_out);
  and and_41 (_4_3, S1, and_42_out);
  and and_42 (and_42_out, _4, not_2_out);
  and and_43 (_5_3, S1, and_44_out);
  and and_44 (and_44_out, _5, not_2_out);
  and and_45 (_6_3, S1, and_46_out);
  and and_46 (and_46_out, _6, not_2_out);
  and and_47 (_7_3, S1, and_48_out);
  and and_48 (and_48_out, _7, not_2_out);
endmodule

module X (
  input  _7,
  input  _6,
  input  _5,
  input  _4,
  input  _3,
  input  _2,
  input  _1,
  input  _0,
  output _0_2,
  output _1_2,
  output _2_2,
  output _3_2,
  output _4_2,
  output _5_2,
  output _6_2,
  output _7_2
);


  assign _0_2 = _0;
  assign _1_2 = _1;
  assign _2_2 = _2;
  assign _3_2 = _3;
  assign _4_2 = _4;
  assign _5_2 = _5;
  assign _6_2 = _6;
  assign _7_2 = _7;
endmodule

module Control_Unit (
  input  Not_Equal,
  input  _7,
  input  _6,
  input  _5,
  input  _4,
  input  _3,
  input  _2,
  input  _1,
  input  _0,
  input  B_Greater_A,
  input  A_Greater_B,
  input  Carry_Out,
  input  Nero,
  input  Input_Available,
  input  Negative,
  input  Reset,
  input  One_by_One,
  input  Clock,
  input  Next_Instruction,
  output M_Clock,
  output Display_Clock,
  output MP_MAR_S2,
  output MP_MAR_S1,
  output MP_MAR_S0,
  output IR_Reset,
  output IR_Clock,
  output Reset_IO,
  output Read_Input,
  output MP_ALU_A_S0,
  output MP_ALU_A_S1,
  output MP_ALU_B_S0,
  output MP_ALU_B_S1,
  output PC_Set,
  output PC_Count,
  output Set_MAR_Add_MBR,
  output Clock_B_Greater_A,
  output Clock_CCR,
  output Set_Carry_Selector,
  output Set_Carry_Data,
  output MP_PC_S0,
  output MAR_Clock,
  output MBR_Clock,
  output MP_PC_S1,
  output Acc_X_Clock,
  output Acc_A_Clock,
  output Acc_B_Clock,
  output Acc_Y_Clock,
  output A_Clock,
  output Stack_Pop,
  output Stack_Push,
  output Stack_Reset,
  output MAR_Reset,
  output MBR_Reset,
  output AX_Reset,
  output AA_Reset,
  output AB_Reset,
  output AY_Reset,
  output A_Reset,
  output A_Invert,
  output B_Invert,
  output AND,
  output OR,
  output A,
  output B,
  output Shift_A_Right,
  output Shift_B_Right,
  output Shift_Loop,
  output Shift_A_Left,
  output Shift_B_Left,
  output XOR,
  output Increment,
  output ADD,
  output X_Invert,
  output Multiply
);

  wire and_1_out, and_2_out, and_3_out, and_4_out, and_5_out, and_6_out, and_7_out, and_8_out, and_9_out,
       and_11_out, and_12_out, and_13_out, and_14_out, and_15_out, and_16_out, and_17_out, button_1_out,
       button_2_out, Condition_x, d_ff_5_q, d_ff_6_q, d_ff_7_q, n1_bit_counter_2_increment_out,
       n1_bit_counter_2_set_out, n1_bit_counter_3_increment_out, n1_bit_counter_3_set_out,
       n1_bit_counter_4_increment_out, n1_bit_counter_4_set_out, n1_bit_counter_5_increment_out,
       n1_bit_counter_5_set_out, n1_bit_counter_6_increment_out, n1_bit_counter_6_set_out,
       n1_bit_counter_7_increment_out, n1_bit_counter_7_set_out, n1_bit_equator_1_x, n1_bit_equator_2_x,
       n1_bit_equator_3_x, n1_bit_equator_4_x, n1_bit_equator_5_x, n2_bit_equator_1_equal,
       n3_bit_demultiplexer_1__0_2, n3_bit_demultiplexer_1__0_3, n3_bit_demultiplexer_1__1_2,
       n3_bit_demultiplexer_1__1_3, n3_bit_demultiplexer_1__2_2, n3_bit_demultiplexer_1__2_3,
       n3_bit_equator_1_equal, n8_bit_register_1__0_3, n8_bit_register_1__1_2, n8_bit_register_1__2_2,
       n8_bit_register_1__3_2, n8_bit_register_1__4_2, n8_bit_register_1__5_2, n8_bit_register_1__6_2,
       n8_way_demultiplex_1__1, n8_way_demultiplex_1__2, n8_way_demultiplex_1__3, n8_way_demultiplex_1__4,
       n8_way_demultiplex_1__5, n8_way_demultiplex_1__7, not_1_out, not_2_out, not_4_out, or_2_out, or_3_out,
       or_4_out, or_5_out, or_6_out, or_7_out, or_8_out, or_9_out, or_10_out, or_11_out, or_12_out,
       or_13_out, or_14_out, or_15_out, or_16_out, or_17_out, or_18_out, or_19_out, or_20_out, or_22_out,
       Target_x;
  wire [6:0] n1_bit_counter_5_out;
  wire [31:0] rom_1_data;
  wire [31:1] and_10_out;
  wire [31:16] rom_2_data;
  wire [31:31] not_3_out;

  or or_1 (A_Reset, Reset, and_10_out[15]);
  D_Latch d_latch_1 (.Clock(or_3_out), .Data(rom_2_data[27]), .Out(MP_ALU_A_S0));
  D_Latch d_latch_2 (.Clock(or_3_out), .Data(rom_2_data[28]), .Out(MP_ALU_A_S1));
  D_Latch d_latch_3 (.Clock(or_3_out), .Data(rom_2_data[25]), .Out(MP_ALU_B_S0));
  D_Latch d_latch_4 (.Clock(or_3_out), .Data(rom_2_data[26]), .Out(MP_ALU_B_S1));
  D_Flip_Flop d_ff_1 (.Q(Set_MAR_Add_MBR), .preset(and_10_out[18]), .reset(or_2_out));  // open: clk, D, Qn, en
  or or_2 (or_2_out, Reset, MBR_Clock);
  or or_3 (or_3_out, Reset, and_10_out[5]);
  _8_bit_Register u_8_bit_register_1 (
    ._6(and_10_out[25]), ._5(and_10_out[26]), ._4(and_10_out[27]), ._3(and_10_out[28]), ._2(and_10_out[29]),
    ._1(and_10_out[30]), ._0(and_10_out[31]), ._0_3(n8_bit_register_1__0_3), ._1_2(n8_bit_register_1__1_2),
    ._2_2(n8_bit_register_1__2_2), ._3_2(n8_bit_register_1__3_2), ._4_2(n8_bit_register_1__4_2),
    ._5_2(n8_bit_register_1__5_2), ._6_2(n8_bit_register_1__6_2), .Clock(not_1_out), .Reset(or_6_out));  // open: _7, _7_2, _0_2
  D_Flip_Flop d_ff_2 (.Q(MP_MAR_S2), .preset(n3_bit_demultiplexer_1__2_2), .reset(or_4_out));  // open: clk, D, Qn, en
  _1_bit_Counter u_1_bit_counter_1 (
    .Increment(n1_bit_counter_3_increment_out), .Set(n1_bit_counter_3_set_out),
    .Out(n1_bit_counter_5_out[6]), .Data(and_2_out));  // open: Increment_Out, Set_Out
  and and_1 (and_1_out, n8_bit_register_1__1_2, not_2_out);
  and and_2 (and_2_out, n8_bit_register_1__0_3, not_2_out);
  D_Flip_Flop d_ff_3 (.Q(MP_MAR_S1), .preset(n3_bit_demultiplexer_1__1_2), .reset(or_4_out));  // open: clk, D, Qn, en
  _8_way_Demultiplex Terget (
    .Data(and_10_out[10]), ._1(Acc_A_Clock), ._2(Acc_B_Clock), ._3(Acc_X_Clock), ._4(Acc_Y_Clock),
    ._5(M_Clock), ._7(Display_Clock), .S2(rom_2_data[24]), .S1(rom_2_data[23]), .S0(rom_2_data[22]));  // open: _0, _6
  _1_bit_Counter u_1_bit_counter_2 (
    .Increment_Out(n1_bit_counter_2_increment_out), .Set_Out(n1_bit_counter_2_set_out),
    .Increment(n1_bit_counter_4_increment_out), .Set(n1_bit_counter_4_set_out),
    .Out(n1_bit_counter_5_out[4]), .Data(and_4_out));
  _1_bit_Counter u_1_bit_counter_3 (
    .Increment_Out(n1_bit_counter_3_increment_out), .Set_Out(n1_bit_counter_3_set_out),
    .Increment(n1_bit_counter_2_increment_out), .Set(n1_bit_counter_2_set_out),
    .Out(n1_bit_counter_5_out[5]), .Data(and_1_out));
  _1_bit_Counter u_1_bit_counter_4 (
    .Increment_Out(n1_bit_counter_4_increment_out), .Set_Out(n1_bit_counter_4_set_out),
    .Increment(n1_bit_counter_7_increment_out), .Set(n1_bit_counter_7_set_out),
    .Out(n1_bit_counter_5_out[3]), .Data(and_3_out));
  and and_3 (and_3_out, n8_bit_register_1__3_2, not_2_out);
  and and_4 (and_4_out, n8_bit_register_1__2_2, not_2_out);
  D_Flip_Flop d_ff_4 (.Q(MP_MAR_S0), .preset(n3_bit_demultiplexer_1__0_2), .reset(or_4_out));  // open: clk, D, Qn, en
  or or_4 (or_4_out, Reset, and_5_out);
  and and_5 (and_5_out, and_9_out, n3_bit_demultiplexer_1__1_2);
  _1_bit_Counter u_1_bit_counter_5 (
    .Increment_Out(n1_bit_counter_5_increment_out), .Set_Out(n1_bit_counter_5_set_out),
    .Increment(and_14_out), .Set(or_5_out), .Out(n1_bit_counter_5_out[0]), .Data(and_8_out));
  _1_bit_Counter u_1_bit_counter_6 (
    .Increment_Out(n1_bit_counter_6_increment_out), .Set_Out(n1_bit_counter_6_set_out),
    .Increment(n1_bit_counter_5_increment_out), .Set(n1_bit_counter_5_set_out),
    .Out(n1_bit_counter_5_out[1]), .Data(and_7_out));
  _1_bit_Counter u_1_bit_counter_7 (
    .Increment_Out(n1_bit_counter_7_increment_out), .Set_Out(n1_bit_counter_7_set_out),
    .Increment(n1_bit_counter_6_increment_out), .Set(n1_bit_counter_6_set_out),
    .Out(n1_bit_counter_5_out[2]), .Data(and_6_out));
  and and_6 (and_6_out, n8_bit_register_1__4_2, not_2_out);
  and and_7 (and_7_out, n8_bit_register_1__5_2, not_2_out);
  and and_8 (and_8_out, n8_bit_register_1__6_2, not_2_out);
  and and_9 (and_9_out, n3_bit_demultiplexer_1__2_2, n3_bit_demultiplexer_1__0_2);
  _3_bit_Demultiplexer u_3_bit_demultiplexer_1 (
    ._0_3(n3_bit_demultiplexer_1__0_3), ._1_3(n3_bit_demultiplexer_1__1_3),
    ._2_3(n3_bit_demultiplexer_1__2_3), ._2_2(n3_bit_demultiplexer_1__2_2),
    ._1_2(n3_bit_demultiplexer_1__1_2), ._0_2(n3_bit_demultiplexer_1__0_2), ._2(and_10_out[9]),
    ._1(and_10_out[8]), ._0(and_10_out[7]), .S(and_10_out[6]));
  not not_1 (not_1_out, and_14_out);
  not not_2 (not_2_out, or_6_out);
  assign {and_10_out[31:17], Read_Input, and_10_out[15], A_Clock, MBR_Clock, MAR_Clock, and_10_out[11:5], IR_Clock, Stack_Pop, Stack_Push, and_10_out[1], PC_Count} = rom_1_data & {32{not_3_out[31]}};  // AND_Gate and_10, 32 bits wide
  ROM #(.addrWidth(7), .dataWidth(32)) rom_1 (.addr(n1_bit_counter_5_out), .data(rom_1_data));  // open: sel
  or or_5 (or_5_out, and_11_out, or_6_out);
  or or_6 (or_6_out, button_1_out, Reset);
  and and_11 (and_11_out, and_14_out, or_16_out);
  not not_3 (not_3_out[31], and_14_out);
  and and_12 (and_12_out, and_10_out[11], One_by_One);
  Button button_1 (.out(button_1_out));
  or or_7 (or_7_out, rom_2_data[24], rom_2_data[23]);
  _8_way_Demultiplex u_8_way_demultiplex_1 (
    .Data(1'b1), ._1(n8_way_demultiplex_1__1), ._2(n8_way_demultiplex_1__2), ._3(n8_way_demultiplex_1__3),
    ._4(n8_way_demultiplex_1__4), ._5(n8_way_demultiplex_1__5), ._7(n8_way_demultiplex_1__7),
    .S2(and_10_out[21]), .S1(and_10_out[20]), .S0(and_10_out[19]));  // open: _0, _6
  and and_13 (and_13_out, d_ff_6_q, and_15_out);
  and and_14 (and_14_out, and_13_out, d_ff_5_q);
  D_Flip_Flop d_ff_5 (.clk(and_12_out), .D(1'b0), .Q(d_ff_5_q), .preset(or_8_out));  // open: Qn, en, reset
  or or_8 (or_8_out, Next_Instruction, Reset);
  or or_9 (or_9_out, or_7_out, rom_2_data[22]);
  _2_bit_Equator u_2_bit_equator_1 (
    .Active(n8_way_demultiplex_1__1), .A0(and_10_out[22]), .A1(and_10_out[23]),
    .Equal(n2_bit_equator_1_equal), .B1(rom_2_data[20]), .B0(rom_2_data[19]));
  _1_bit_Equator Target (._1(and_10_out[24]), ._0(or_9_out), .Active(n8_way_demultiplex_1__4), .X(Target_x));
  _1_bit_Equator Condition (._1(and_10_out[24]), ._0(or_19_out), .Active(n8_way_demultiplex_1__5), .X(Condition_x));
  D_Flip_Flop d_ff_6 (.clk(and_10_out[17]), .D(1'b0), .Q(d_ff_6_q), .preset(or_10_out));  // open: Qn, en, reset
  or or_10 (or_10_out, Input_Available, Reset);
  and and_15 (and_15_out, or_11_out, d_ff_7_q);
  D_Flip_Flop d_ff_7 (.Q(d_ff_7_q), .preset(Reset), .reset(and_17_out));  // open: clk, D, Qn, en
  ROM #(.dataWidth(32)) rom_2 (
    .addr({_7, _6, _5, _4, _3, _2, _1, _0}),
    .data({rom_2_data, Multiply, A_Invert, B_Invert, AND, OR, A, B, Shift_A_Right, Shift_B_Right, Shift_Loop, Shift_A_Left, Shift_B_Left, XOR, Increment, ADD, X_Invert}));  // open: sel
  _3_bit_Equator u_3_bit_equator_1 (
    .Active(n8_way_demultiplex_1__2), .A0(and_10_out[22]), .A1(and_10_out[23]), .A2(and_10_out[24]),
    .Equal(n3_bit_equator_1_equal), .B2(rom_2_data[31]), .B1(rom_2_data[30]), .B0(rom_2_data[29]));
  Button button_2 (.out(button_2_out));
  or or_11 (or_11_out, button_2_out, Clock);
  _1_bit_Equator u_1_bit_equator_1 (
    ._1(and_10_out[22]), ._0(rom_2_data[21]), .Active(n8_way_demultiplex_1__3), .X(n1_bit_equator_1_x));
  or or_12 (or_12_out, n3_bit_equator_1_equal, n2_bit_equator_1_equal);
  or or_13 (or_13_out, n1_bit_equator_1_x, or_12_out);
  or or_14 (or_14_out, Condition_x, or_13_out);
  or or_15 (or_15_out, n8_way_demultiplex_1__7, or_14_out);
  or or_16 (or_16_out, Target_x, or_15_out);
  and and_16 (and_16_out, rom_2_data[30], rom_2_data[31]);
  and and_17 (and_17_out, rom_2_data[29], and_16_out);
  _1_bit_Equator u_1_bit_equator_2 (._1(XOR), ._0(B_Greater_A), .Active(Increment), .X(n1_bit_equator_2_x));
  _1_bit_Equator u_1_bit_equator_3 (._1(Shift_A_Left), ._0(A_Greater_B), .Active(Shift_B_Left), .X(n1_bit_equator_3_x));
  _1_bit_Equator u_1_bit_equator_4 (._1(Shift_B_Right), ._0(Carry_Out), .Active(Shift_Loop), .X(n1_bit_equator_4_x));
  or or_17 (or_17_out, n1_bit_equator_4_x, n1_bit_equator_3_x);
  or or_18 (or_18_out, Shift_A_Right, or_17_out);
  or or_19 (or_19_out, or_18_out, or_20_out);
  _1_bit_Equator u_1_bit_equator_5 (._1(ADD), ._0(not_4_out), .Active(X_Invert), .X(n1_bit_equator_5_x));
  or or_20 (or_20_out, n1_bit_equator_2_x, n1_bit_equator_5_x);
  not not_4 (not_4_out, Not_Equal);
  or or_21 (Clock_CCR, A_Clock, Reset);
  or or_22 (or_22_out, n3_bit_demultiplexer_1__2_3, Reset);
  or or_23 (PC_Set, Reset, and_10_out[1]);
  D_Flip_Flop d_ff_8 (.Q(MP_PC_S0), .preset(n3_bit_demultiplexer_1__0_3), .reset(or_22_out));  // open: clk, D, Qn, en
  D_Flip_Flop d_ff_9 (.Q(MP_PC_S1), .preset(n3_bit_demultiplexer_1__1_3), .reset(or_22_out));  // open: clk, D, Qn, en

  assign AA_Reset = Reset;
  assign AB_Reset = Reset;
  assign AX_Reset = Reset;
  assign AY_Reset = Reset;
  assign IR_Reset = Reset;
  assign MAR_Reset = Reset;
  assign MBR_Reset = Reset;
  assign Reset_IO = Reset;
  assign Stack_Reset = Reset;

  // Notes on the sheet:
  //   contents of rom_1 (hex, n*v repeats v):
  //   380 200 1000 2000 10 36080000 1 1000 2000 18880000 20c80000 28380000 380 100 40000 28380000 380 280
  //   40000 0 1000 2000 36180000 380 80 1000 2000 20 7a100000 46500000 4a900000 5ed00000 6b100000 77500000
  //   0 4000 7a380000 1 7a280000 380 200 1000 2000 240 140 2 7e380000 1 4 240 140 2 7e380000 8 240 1c0 2 0
  //   7e380000 10000 20000 400 1 8000 800 380000
  //   contents of rom_2 (hex, n*v repeats v):
  //   0 60080000 60280000 80000000 e0000000 2e408000 2e808000 32c08000 33008000 2a408000 2b008000 36c08000
  //   36808000 2c488000 2c688000 2c508000 2c588000 2e400002 2e800002 32c00002 33000002 2a400002 2b000002
  //   36c00002 36800002 2c480002 2c680002 2c500002 2c580002 2e402006 2e804006 32c02006 33004006 2c682006
  //   2c482006 2c502006 2c582006 28400006 26800006 30c00006 23000006 23680006 23500006 23580006 28402002
  //   26804002 30c02002 23004002 25684002 25504002 25584002 24480200 24680200 24500200 24580200 24880200
  //   24a80200 24900200 24980200 24c80200 24e80200 24d00200 24d80200 25080200 25280200 25100200 25180200
  //   29680400 27680200 31680400 23680200 29500400 27500200 31500400 23500200 29580400 27580200 31580400
  //   23580200 29c00400 27c00200 31c00400 23c00200 25c80200 25e80200 25d00200 25d80200 38400400 38800200
  //   a0000000 28800400 26400200 31000400 22c00200 28c00400 30400400 27000200 22800200 29000400 22400200
  //   30800400 26c00200 28400100 28400020 26800080 26800010 28400140 28400060 268000c0 26800050 0 0
  //   2e000000 32000000 2c080000 2c280000 2c100000 2c180000 40000100 40000000 40000000 40000003 40000001
  //   4000000c 40000030 4000000f 40000033 28404400 26802200 30c04400 23002200 25682200 25502200 25582200
  //   28404003 26802003 30c04003 23002003 25682003 25502003 25582003 2e401000 2e400800 2e400008 32c01000
  //   32c00800 32c00008 20400000 20800000 20c00000 21000000 21680000 21500000 21580000 20000000
endmodule

module _3_Way_Multiplexor (
  input  _7,
  input  _6,
  input  _5,
  input  _4,
  input  _3,
  input  _2,
  input  _1,
  input  _0,
  input  _0_2,
  input  _0_3,
  input  _1_2,
  input  _1_3,
  input  _2_2,
  input  _2_3,
  input  _3_2,
  input  _3_3,
  input  _4_2,
  input  _4_3,
  input  _5_2,
  input  _5_3,
  input  _6_2,
  input  _6_3,
  input  _7_2,
  input  _7_3,
  input  S0,
  input  S1,
  output _7_4,
  output _6_4,
  output _5_4,
  output _4_4,
  output _3_4,
  output _2_4,
  output _1_4,
  output _0_4
);

  wire and_1_out, and_2_out, and_3_out, and_4_out, and_5_out, and_6_out, and_7_out, and_8_out, and_9_out,
       and_10_out, and_11_out, and_12_out, and_13_out, and_14_out, and_15_out, and_16_out, and_17_out,
       and_18_out, and_19_out, and_20_out, and_21_out, and_22_out, and_23_out, and_24_out, and_25_out,
       and_26_out, and_27_out, and_28_out, and_29_out, and_30_out, and_31_out, and_32_out, and_33_out,
       and_34_out, and_35_out, and_36_out, and_37_out, and_38_out, and_39_out, and_40_out, and_41_out,
       and_42_out, and_43_out, and_44_out, and_45_out, and_46_out, and_47_out, and_48_out, not_1_out,
       not_2_out, not_3_out, or_1_out, or_3_out, or_4_out, or_7_out, or_8_out, or_11_out, or_12_out,
       or_15_out;

  not not_1 (not_1_out, S1);
  and and_1 (and_1_out, _0_2, not_1_out);
  and and_2 (and_2_out, _1_2, not_1_out);
  and and_3 (and_3_out, _2_2, not_1_out);
  and and_4 (and_4_out, _3_2, not_1_out);
  and and_5 (and_5_out, _4_2, not_1_out);
  and and_6 (and_6_out, _5_2, not_1_out);
  and and_7 (and_7_out, _6_2, not_1_out);
  and and_8 (and_8_out, _7_2, not_1_out);
  not not_2 (not_2_out, not_3_out);
  and and_9 (and_9_out, not_3_out, and_19_out);
  and and_10 (and_10_out, not_2_out, and_1_out);
  and and_11 (and_11_out, not_2_out, and_2_out);
  and and_12 (and_12_out, not_2_out, and_3_out);
  and and_13 (and_13_out, not_2_out, and_4_out);
  and and_14 (and_14_out, not_2_out, and_5_out);
  and and_15 (and_15_out, not_2_out, and_6_out);
  and and_16 (and_16_out, not_2_out, and_7_out);
  and and_17 (and_17_out, not_2_out, and_8_out);
  or or_1 (or_1_out, and_40_out, and_9_out);
  or or_2 (_7_4, and_17_out, or_1_out);
  and and_18 (and_18_out, _6, S1);
  and and_19 (and_19_out, _7, S1);
  and and_20 (and_20_out, not_3_out, and_22_out);
  and and_21 (and_21_out, not_3_out, and_18_out);
  or or_3 (or_3_out, and_38_out, and_20_out);
  or or_4 (or_4_out, and_39_out, and_21_out);
  or or_5 (_5_4, and_15_out, or_3_out);
  or or_6 (_6_4, and_16_out, or_4_out);
  and and_22 (and_22_out, _5, S1);
  and and_23 (and_23_out, _4, S1);
  and and_24 (and_24_out, not_3_out, and_23_out);
  and and_25 (and_25_out, not_3_out, and_27_out);
  or or_7 (or_7_out, and_36_out, and_25_out);
  or or_8 (or_8_out, and_37_out, and_24_out);
  or or_9 (_4_4, and_14_out, or_8_out);
  or or_10 (_3_4, and_13_out, or_7_out);
  and and_26 (and_26_out, _2, S1);
  and and_27 (and_27_out, _3, S1);
  and and_28 (and_28_out, not_3_out, and_31_out);
  and and_29 (and_29_out, not_3_out, and_26_out);
  or or_11 (or_11_out, and_34_out, and_28_out);
  or or_12 (or_12_out, and_35_out, and_29_out);
  or or_13 (_1_4, and_11_out, or_11_out);
  or or_14 (_2_4, and_12_out, or_12_out);
  and and_30 (and_30_out, _0, S1);
  and and_31 (and_31_out, _1, S1);
  and and_32 (and_32_out, not_3_out, and_30_out);
  and and_33 (and_33_out, S0, and_41_out);
  and and_34 (and_34_out, S0, and_42_out);
  and and_35 (and_35_out, S0, and_43_out);
  and and_36 (and_36_out, S0, and_44_out);
  and and_37 (and_37_out, S0, and_45_out);
  and and_38 (and_38_out, S0, and_46_out);
  and and_39 (and_39_out, S0, and_47_out);
  and and_40 (and_40_out, S0, and_48_out);
  or or_15 (or_15_out, and_33_out, and_32_out);
  or or_16 (_0_4, and_10_out, or_15_out);
  not not_3 (not_3_out, S0);
  and and_41 (and_41_out, _0_3, S1);
  and and_42 (and_42_out, _1_3, S1);
  and and_43 (and_43_out, _2_3, S1);
  and and_44 (and_44_out, _3_3, S1);
  and and_45 (and_45_out, _4_3, S1);
  and and_46 (and_46_out, _5_3, S1);
  and and_47 (and_47_out, _6_3, S1);
  and and_48 (and_48_out, _7_3, S1);
endmodule

module _8_bit_Counter (
  input  Increment,
  input  Set,
  input  _7,
  input  _6,
  input  _5,
  input  _4,
  input  _3,
  input  _2,
  input  _1,
  input  _0,
  output _7_2,
  output _6_2,
  output _5_2,
  output _4_2,
  output _3_2,
  output _2_2,
  output _1_2,
  output _0_2,
  output Increment_Out,
  output Set_Carry
);

  wire and_1_out, and_2_out, and_3_out, and_4_out, and_5_out, and_6_out, and_7_out, and_8_out, and_9_out,
       and_10_out, and_11_out, and_12_out, and_13_out, and_14_out, and_15_out, and_16_out, not_1_out,
       not_2_out, not_3_out, not_4_out, not_5_out, not_6_out, not_7_out, not_8_out, t_ff_2_qn, t_ff_3_qn,
       t_ff_4_qn, t_ff_5_qn, t_ff_6_qn, t_ff_7_qn, t_ff_8_qn;

  and and_1 (and_1_out, Set, _7);
  not not_1 (not_1_out, _7);
  T_Flip_Flop t_ff_1 (
    .clk(t_ff_2_qn), .T(t_ff_2_qn), .Q(_7_2), .Qn(Increment_Out), .preset(and_1_out), .reset(and_3_out));  // open: en
  and and_2 (and_2_out, Set, _6);
  and and_3 (and_3_out, not_1_out, Set);
  not not_2 (not_2_out, _6);
  T_Flip_Flop t_ff_2 (
    .clk(t_ff_3_qn), .T(t_ff_3_qn), .Q(_6_2), .Qn(t_ff_2_qn), .preset(and_2_out), .reset(and_5_out));  // open: en
  and and_4 (and_4_out, Set, _5);
  and and_5 (and_5_out, not_2_out, Set);
  not not_3 (not_3_out, _5);
  T_Flip_Flop t_ff_3 (
    .clk(t_ff_4_qn), .T(t_ff_4_qn), .Q(_5_2), .Qn(t_ff_3_qn), .preset(and_4_out), .reset(and_7_out));  // open: en
  and and_6 (and_6_out, Set, _4);
  and and_7 (and_7_out, not_3_out, Set);
  not not_4 (not_4_out, _4);
  T_Flip_Flop t_ff_4 (
    .clk(t_ff_5_qn), .T(t_ff_5_qn), .Q(_4_2), .Qn(t_ff_4_qn), .preset(and_6_out), .reset(and_9_out));  // open: en
  and and_8 (and_8_out, Set, _3);
  and and_9 (and_9_out, not_4_out, Set);
  not not_5 (not_5_out, _3);
  T_Flip_Flop t_ff_5 (
    .clk(t_ff_6_qn), .T(t_ff_6_qn), .Q(_3_2), .Qn(t_ff_5_qn), .preset(and_8_out), .reset(and_10_out));  // open: en
  and and_10 (and_10_out, not_5_out, Set);
  and and_11 (and_11_out, Set, _2);
  not not_6 (not_6_out, _2);
  T_Flip_Flop t_ff_6 (
    .clk(t_ff_7_qn), .T(t_ff_7_qn), .Q(_2_2), .Qn(t_ff_6_qn), .preset(and_11_out), .reset(and_13_out));  // open: en
  and and_12 (and_12_out, Set, _1);
  and and_13 (and_13_out, not_6_out, Set);
  not not_7 (not_7_out, _1);
  T_Flip_Flop t_ff_7 (
    .clk(t_ff_8_qn), .T(t_ff_8_qn), .Q(_1_2), .Qn(t_ff_7_qn), .preset(and_12_out), .reset(and_14_out));  // open: en
  and and_14 (and_14_out, not_7_out, Set);
  and and_15 (and_15_out, Set, _0);
  not not_8 (not_8_out, _0);
  T_Flip_Flop t_ff_8 (
    .clk(Increment), .T(Increment), .Q(_0_2), .Qn(t_ff_8_qn), .preset(and_15_out), .reset(and_16_out));  // open: en
  and and_16 (and_16_out, not_8_out, Set);

  assign Set_Carry = Set;
endmodule

module S_R_Latch (
  input  Set,
  input  Data,
  input  Reset,
  input  Clock,
  output X
);

  wire and_1_out, and_2_out, and_3_out, and_4_out, not_1_out, not_2_out, not_3_out, or_1_out, or_2_out,
       or_3_out, or_4_out, or_5_out;

  not not_1 (not_1_out, Data);
  or or_1 (or_1_out, Set, Reset);
  not not_2 (not_2_out, or_1_out);
  or or_2 (or_2_out, Set, and_1_out);
  and and_1 (and_1_out, Data, not_2_out);
  and and_2 (and_2_out, not_2_out, not_1_out);
  or or_3 (or_3_out, and_2_out, Reset);
  and and_3 (and_3_out, Clock, or_2_out);
  or or_4 (or_4_out, and_3_out, X);
  or or_5 (or_5_out, not_3_out, and_4_out);
  and and_4 (and_4_out, or_3_out, Clock);
  not not_3 (not_3_out, or_4_out);
  not not_4 (X, or_5_out);
endmodule

module bit_Multiplexor (
  input  _1,
  input  _0,
  input  S,
  output X
);

  wire and_1_out, and_2_out;

  and and_1 (and_1_out, _1, S);
  and and_2 (and_2_out, _0, S);
  or or_1 (X, and_1_out, and_2_out);
endmodule

// C
module _1_bit_Counter (
  input  Increment,
  input  Set,
  input  Data,
  output Out,
  output Increment_Out,
  output Set_Out
);

  wire and_1_out, and_2_out, not_1_out;

  T_Flip_Flop t_ff_1 (
    .clk(Increment), .T(Increment), .Q(Out), .Qn(Increment_Out), .preset(and_2_out), .reset(and_1_out));  // open: en
  and and_1 (and_1_out, not_1_out, Set);
  and and_2 (and_2_out, Set, Data);
  not not_1 (not_1_out, Data);

  assign Set_Out = Set;
endmodule

module _8_bit_Stack (
  input  Reset,
  input  Push,
  input  _7,
  input  _5,
  input  _3,
  input  _1,
  input  Pop,
  input  _6,
  input  _4,
  input  _2,
  input  _0,
  output _0_2,
  output _1_2,
  output _2_2,
  output _3_2,
  output _4_2,
  output _5_2,
  output _6_2,
  output _7_2
);

  wire not_1_out;
  wire [7:0] n8_bit_counter_inc_dec_1__0;

  _8_bit_Counter__Inc_Dec u_8_bit_counter_inc_dec_1 (
    ._0(n8_bit_counter_inc_dec_1__0[0]), ._1(n8_bit_counter_inc_dec_1__0[1]),
    ._2(n8_bit_counter_inc_dec_1__0[2]), ._3(n8_bit_counter_inc_dec_1__0[3]),
    ._4(n8_bit_counter_inc_dec_1__0[4]), ._5(n8_bit_counter_inc_dec_1__0[5]),
    ._6(n8_bit_counter_inc_dec_1__0[6]), ._7(n8_bit_counter_inc_dec_1__0[7]), .Reset(Reset),
    .Increment(Push), .Decrement(Pop));  // open: Carry_Out
  RAM #(.bus("separate")) ram_1 (
    .addr(n8_bit_counter_inc_dec_1__0), .din({_7, _6, _5, _4, _3, _2, _1, _0}),
    .data({_7_2, _6_2, _5_2, _4_2, _3_2, _2_2, _1_2, _0_2}), .clk(Push), .ld(not_1_out), .clr(Reset));  // open: str, sel
  not not_1 (not_1_out, Push);
endmodule
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module LED_Matrix_Controller (
  input  Value,
  input  Clear,
  input  Clock,
  input  in_4,
  input  in_5,
  input  in_6,
  input  in_7,
  input  in_8,
  input  in_9,
  input  in_10,
  input  in_11,
  output [15:0] out_12,
  output [15:0] out_13,
  output [15:0] out_14,
  output [15:0] out_15,
  output [15:0] out_16,
  output [15:0] out_17,
  output [15:0] out_18,
  output [15:0] out_19,
  output [15:0] out_20,
  output [15:0] out_21,
  output [15:0] out_22,
  output [15:0] out_23,
  output [15:0] out_24,
  output [15:0] out_25,
  output [15:0] out_26,
  output [15:0] out_27
);

  wire [15:0] and_1_out, and_2_out, and_3_out, and_4_out, and_5_out, and_6_out, and_7_out, and_8_out,
       and_9_out, and_10_out, and_11_out, and_12_out, and_13_out, and_14_out, and_15_out, and_16_out,
       and_17_out, and_18_out, and_19_out, and_20_out, and_21_out, and_22_out, and_23_out, and_24_out,
       and_25_out, and_26_out, and_27_out, and_28_out, and_29_out, and_30_out, and_31_out, and_32_out,
       and_33_out, bit_extender_1_out, bit_extender_2_out, decoder_1_out0, decoder_2_out0, not_1_out,
       not_2_out, not_3_out, not_4_out, not_5_out, not_6_out, not_7_out, not_8_out, not_9_out, not_10_out,
       not_11_out, not_12_out, not_13_out, not_14_out, not_15_out, not_16_out, or_1_out, or_2_out, or_3_out,
       or_4_out, or_5_out, or_6_out, or_7_out, or_8_out, or_9_out, or_10_out, or_11_out, or_12_out,
       or_13_out, or_14_out, or_15_out, or_16_out;

  Decoder #(.select(4), .enable("false")) decoder_1 (
    .out0(decoder_1_out0[0]), .out1(decoder_1_out0[1]), .out2(decoder_1_out0[2]), .out3(decoder_1_out0[3]),
    .out4(decoder_1_out0[4]), .out5(decoder_1_out0[5]), .out6(decoder_1_out0[6]), .out7(decoder_1_out0[7]),
    .out8(decoder_1_out0[8]), .out9(decoder_1_out0[9]), .out10(decoder_1_out0[10]),
    .out11(decoder_1_out0[11]), .out12(decoder_1_out0[12]), .out13(decoder_1_out0[13]),
    .out14(decoder_1_out0[14]), .out15(decoder_1_out0[15]), .sel({in_4, in_5, in_6, in_7}));
  Decoder #(.select(4), .enable("false")) decoder_2 (
    .out0(decoder_2_out0[0]), .out1(decoder_2_out0[1]), .out2(decoder_2_out0[2]), .out3(decoder_2_out0[3]),
    .out4(decoder_2_out0[4]), .out5(decoder_2_out0[5]), .out6(decoder_2_out0[6]), .out7(decoder_2_out0[7]),
    .out8(decoder_2_out0[8]), .out9(decoder_2_out0[9]), .out10(decoder_2_out0[10]),
    .out11(decoder_2_out0[11]), .out12(decoder_2_out0[12]), .out13(decoder_2_out0[13]),
    .out14(decoder_2_out0[14]), .out15(decoder_2_out0[15]), .sel({in_8, in_9, in_10, in_11}));
  assign bit_extender_1_out = {{15{Clock}}, Clock};  // Bit_Extender bit_extender_1
  assign and_1_out = bit_extender_1_out & decoder_2_out0;  // AND_Gate and_1, 16 bits wide
  assign bit_extender_2_out = {{15{Value}}, Value};  // Bit_Extender bit_extender_2
  assign and_2_out = bit_extender_2_out & decoder_1_out0;  // AND_Gate and_2, 16 bits wide
  assign not_1_out = ~decoder_1_out0;  // NOT_Gate not_1, 16 bits wide
  assign and_3_out = not_1_out & out_12;  // AND_Gate and_3, 16 bits wide
  assign and_4_out = bit_extender_2_out & decoder_1_out0;  // AND_Gate and_4, 16 bits wide
  assign not_2_out = ~decoder_1_out0;  // NOT_Gate not_2, 16 bits wide
  assign and_5_out = not_2_out & out_13;  // AND_Gate and_5, 16 bits wide
  assign and_6_out = bit_extender_2_out & decoder_1_out0;  // AND_Gate and_6, 16 bits wide
  assign not_3_out = ~decoder_1_out0;  // NOT_Gate not_3, 16 bits wide
  assign and_7_out = not_3_out & out_14;  // AND_Gate and_7, 16 bits wide
  assign and_8_out = bit_extender_2_out & decoder_1_out0;  // AND_Gate and_8, 16 bits wide
  assign not_4_out = ~decoder_1_out0;  // NOT_Gate not_4, 16 bits wide
  assign and_9_out = not_4_out & out_15;  // AND_Gate and_9, 16 bits wide
  assign and_10_out = bit_extender_2_out & decoder_1_out0;  // AND_Gate and_10, 16 bits wide
  assign not_5_out = ~decoder_1_out0;  // NOT_Gate not_5, 16 bits wide
  assign and_11_out = not_5_out & out_16;  // AND_Gate and_11, 16 bits wide
  assign and_12_out = bit_extender_2_out & decoder_1_out0;  // AND_Gate and_12, 16 bits wide
  assign not_6_out = ~decoder_1_out0;  // NOT_Gate not_6, 16 bits wide
  assign and_13_out = not_6_out & out_17;  // AND_Gate and_13, 16 bits wide
  assign and_14_out = bit_extender_2_out & decoder_1_out0;  // AND_Gate and_14, 16 bits wide
  assign not_7_out = ~decoder_1_out0;  // NOT_Gate not_7, 16 bits wide
  assign and_15_out = not_7_out & out_18;  // AND_Gate and_15, 16 bits wide
  assign and_16_out = bit_extender_2_out & decoder_1_out0;  // AND_Gate and_16, 16 bits wide
  assign not_8_out = ~decoder_1_out0;  // NOT_Gate not_8, 16 bits wide
  assign and_17_out = not_8_out & out_19;  // AND_Gate and_17, 16 bits wide
  assign and_18_out = bit_extender_2_out & decoder_1_out0;  // AND_Gate and_18, 16 bits wide
  assign not_9_out = ~decoder_1_out0;  // NOT_Gate not_9, 16 bits wide
  assign and_19_out = not_9_out & out_20;  // AND_Gate and_19, 16 bits wide
  assign and_20_out = bit_extender_2_out & decoder_1_out0;  // AND_Gate and_20, 16 bits wide
  assign not_10_out = ~decoder_1_out0;  // NOT_Gate not_10, 16 bits wide
  assign and_21_out = not_10_out & out_21;  // AND_Gate and_21, 16 bits wide
  assign and_22_out = bit_extender_2_out & decoder_1_out0;  // AND_Gate and_22, 16 bits wide
  assign not_11_out = ~decoder_1_out0;  // NOT_Gate not_11, 16 bits wide
  assign and_23_out = not_11_out & out_22;  // AND_Gate and_23, 16 bits wide
  assign and_24_out = bit_extender_2_out & decoder_1_out0;  // AND_Gate and_24, 16 bits wide
  assign not_12_out = ~decoder_1_out0;  // NOT_Gate not_12, 16 bits wide
  assign and_25_out = not_12_out & out_23;  // AND_Gate and_25, 16 bits wide
  assign and_26_out = bit_extender_2_out & decoder_1_out0;  // AND_Gate and_26, 16 bits wide
  assign not_13_out = ~decoder_1_out0;  // NOT_Gate not_13, 16 bits wide
  assign and_27_out = not_13_out & out_24;  // AND_Gate and_27, 16 bits wide
  assign and_28_out = bit_extender_2_out & decoder_1_out0;  // AND_Gate and_28, 16 bits wide
  assign not_14_out = ~decoder_1_out0;  // NOT_Gate not_14, 16 bits wide
  assign and_29_out = not_14_out & out_25;  // AND_Gate and_29, 16 bits wide
  assign and_30_out = bit_extender_2_out & decoder_1_out0;  // AND_Gate and_30, 16 bits wide
  assign not_15_out = ~decoder_1_out0;  // NOT_Gate not_15, 16 bits wide
  assign and_31_out = not_15_out & out_26;  // AND_Gate and_31, 16 bits wide
  assign and_32_out = bit_extender_2_out & decoder_1_out0;  // AND_Gate and_32, 16 bits wide
  assign not_16_out = ~decoder_1_out0;  // NOT_Gate not_16, 16 bits wide
  assign and_33_out = not_16_out & out_27;  // AND_Gate and_33, 16 bits wide
  assign or_1_out = and_2_out | and_3_out;  // OR_Gate or_1, 16 bits wide
  Register_part #(.width(16)) register_1 (.D(or_1_out), .Q(out_12), .clk(and_1_out[0]), .clr(Clear));  // open: en
  assign or_2_out = and_4_out | and_5_out;  // OR_Gate or_2, 16 bits wide
  Register_part #(.width(16)) register_2 (.D(or_2_out), .Q(out_13), .clk(and_1_out[1]), .clr(Clear));  // open: en
  Register_part #(.width(16)) register_3 (.D(or_3_out), .Q(out_14), .clk(and_1_out[2]), .clr(Clear));  // open: en
  assign or_3_out = and_6_out | and_7_out;  // OR_Gate or_3, 16 bits wide
  assign or_4_out = and_8_out | and_9_out;  // OR_Gate or_4, 16 bits wide
  Register_part #(.width(16)) register_4 (.D(or_4_out), .Q(out_15), .clk(and_1_out[3]), .clr(Clear));  // open: en
  assign or_5_out = and_10_out | and_11_out;  // OR_Gate or_5, 16 bits wide
  Register_part #(.width(16)) register_5 (.D(or_5_out), .Q(out_16), .clk(and_1_out[4]), .clr(Clear));  // open: en
  assign or_6_out = and_12_out | and_13_out;  // OR_Gate or_6, 16 bits wide
  Register_part #(.width(16)) register_6 (.D(or_6_out), .Q(out_17), .clk(and_1_out[5]), .clr(Clear));  // open: en
  assign or_7_out = and_14_out | and_15_out;  // OR_Gate or_7, 16 bits wide
  Register_part #(.width(16)) register_7 (.D(or_7_out), .Q(out_18), .clk(and_1_out[6]), .clr(Clear));  // open: en
  Register_part #(.width(16)) register_8 (.D(or_8_out), .Q(out_19), .clk(and_1_out[7]), .clr(Clear));  // open: en
  assign or_8_out = and_16_out | and_17_out;  // OR_Gate or_8, 16 bits wide
  Register_part #(.width(16)) register_9 (.D(or_9_out), .Q(out_20), .clk(and_1_out[8]), .clr(Clear));  // open: en
  assign or_9_out = and_18_out | and_19_out;  // OR_Gate or_9, 16 bits wide
  Register_part #(.width(16)) register_10 (.D(or_10_out), .Q(out_21), .clk(and_1_out[9]), .clr(Clear));  // open: en
  assign or_10_out = and_20_out | and_21_out;  // OR_Gate or_10, 16 bits wide
  assign or_11_out = and_22_out | and_23_out;  // OR_Gate or_11, 16 bits wide
  Register_part #(.width(16)) register_11 (.D(or_11_out), .Q(out_22), .clk(and_1_out[10]), .clr(Clear));  // open: en
  Register_part #(.width(16)) register_12 (.D(or_12_out), .Q(out_23), .clk(and_1_out[11]), .clr(Clear));  // open: en
  assign or_12_out = and_24_out | and_25_out;  // OR_Gate or_12, 16 bits wide
  assign or_13_out = and_26_out | and_27_out;  // OR_Gate or_13, 16 bits wide
  Register_part #(.width(16)) register_13 (.D(or_13_out), .Q(out_24), .clk(and_1_out[12]), .clr(Clear));  // open: en
  Register_part #(.width(16)) register_14 (.D(or_14_out), .Q(out_25), .clk(and_1_out[13]), .clr(Clear));  // open: en
  assign or_14_out = and_28_out | and_29_out;  // OR_Gate or_14, 16 bits wide
  assign or_15_out = and_30_out | and_31_out;  // OR_Gate or_15, 16 bits wide
  Register_part #(.width(16)) register_15 (.D(or_15_out), .Q(out_26), .clk(and_1_out[14]), .clr(Clear));  // open: en
  assign or_16_out = and_32_out | and_33_out;  // OR_Gate or_16, 16 bits wide
  Register_part #(.width(16)) register_16 (.D(or_16_out), .Q(out_27), .clk(and_1_out[15]), .clr(Clear));  // open: en
endmodule
